// Logisim project ALU.circ as structural Verilog: 1 circuit, main circuit ALU
module ALU (
  input  [31:0] SrcA,
  input  [31:0] SrcB,
  input  [3:0] ALU_Control,
  output Zero,
  output [31:0] ALU_Result
);

  wire [31:0] adder_1_out, and_1_out, average_1_out_3, bit_extender_1_out, multiplexer_1_out, not_1_out,
       or_1_out, popcounter32_1_out_2;

  assign not_1_out = ~SrcB;  // NOT_Gate not_1, 32 bits wide
  Multiplexer #(.width(32)) multiplexer_1 (
    .in0(SrcB), .in1(not_1_out), .out(multiplexer_1_out), .sel(ALU_Control[2]));  // open: en
  assign and_1_out = SrcA & multiplexer_1_out;  // AND_Gate and_1, 32 bits wide
  assign or_1_out = SrcA | multiplexer_1_out;  // OR_Gate or_1, 32 bits wide
  Adder #(.width(32)) adder_1 (.a(SrcA), .b(multiplexer_1_out), .out(adder_1_out), .cin(ALU_Control[2]));  // open: cout
  PopCounter32 popcounter32_1 (.in_1(SrcB), .out_2(popcounter32_1_out_2));
  Average average_1 (.in_1(SrcA), .in_2(SrcB), .out_3(average_1_out_3));
  assign bit_extender_1_out = {{31{1'b0}}, adder_1_out[31]};  // Bit_Extender bit_extender_1
  Multiplexer #(.select(3), .width(32)) multiplexer_2 (
    .in0(and_1_out), .in1(or_1_out), .in2(adder_1_out), .in3(bit_extender_1_out), .in4(popcounter32_1_out_2),
    .in5(average_1_out_3), .in7({32{1'b0}}), .out(ALU_Result), .sel({ALU_Control[3], ALU_Control[1:0]}));  // open: in6, en
  Comparator #(.width(32)) comparator_1 (.a({32{1'b0}}), .b(ALU_Result), .eq(Zero));  // open: gt, lt
endmodule
