// Logisim project ALU_Decoder.circ as structural Verilog: 1 circuit, main circuit ALU_Decoder
module ALU_Decoder (
  input  [2:0] ALUOp_2_0,
  input  [5:0] Funct_5_0,
  output [3:0] ALUCtrl_3_0
);

  wire and_1_out, and_2_out, and_3_out, and_4_out, and_5_out, and_6_out, and_7_out, and_8_out, and_9_out,
       and_10_out, and_11_out, and_12_out, and_13_out, and_14_out, and_15_out, and_16_out, and_17_out,
       and_18_out, and_19_out, and_20_out, and_21_out, and_22_out, and_23_out, and_24_out, not_1_out,
       not_2_out, not_3_out, not_4_out, not_5_out, not_6_out, not_7_out, not_8_out, not_9_out, not_10_out,
       not_11_out, not_12_out, not_13_out, not_14_out, not_15_out, not_16_out, not_17_out, not_18_out,
       not_19_out, not_20_out, not_21_out, not_22_out, not_23_out, not_24_out, not_25_out, not_26_out,
       not_27_out, not_28_out, not_29_out, not_30_out, not_31_out, not_32_out, not_33_out, not_34_out,
       not_35_out;

  and and_1 (and_1_out, ALUOp_2_0[1], not_1_out);
  not not_1 (not_1_out, Funct_5_0[5]);
  not not_2 (not_2_out, Funct_5_0[2]);
  and and_2 (and_2_out, ALUOp_2_0[1], not_2_out, Funct_5_0[0]);
  and and_3 (and_3_out, ALUOp_2_0[1], Funct_5_0[2], Funct_5_0[1]);
  and and_4 (and_4_out, ALUOp_2_0[1], Funct_5_0[3], not_3_out);
  not not_3 (not_3_out, Funct_5_0[1]);
  and and_5 (and_5_out, ALUOp_2_0[1], Funct_5_0[4]);
  and and_6 (and_6_out, ALUOp_2_0[1], ALUOp_2_0[0]);
  not not_4 (not_4_out, ALUOp_2_0[1]);
  not not_5 (not_5_out, ALUOp_2_0[0]);
  not not_6 (not_6_out, Funct_5_0[5]);
  not not_7 (not_7_out, ALUOp_2_0[0]);
  not not_8 (not_8_out, Funct_5_0[2]);
  not not_9 (not_9_out, ALUOp_2_0[0]);
  not not_10 (not_10_out, ALUOp_2_0[0]);
  not not_11 (not_11_out, Funct_5_0[4]);
  not not_12 (not_12_out, ALUOp_2_0[0]);
  not not_13 (not_13_out, Funct_5_0[3]);
  not not_14 (not_14_out, ALUOp_2_0[0]);
  not not_15 (not_15_out, Funct_5_0[2]);
  not not_16 (not_16_out, ALUOp_2_0[1]);
  not not_17 (not_17_out, ALUOp_2_0[0]);
  and and_7 (and_7_out, not_17_out, not_18_out);
  not not_18 (not_18_out, Funct_5_0[5]);
  not not_19 (not_19_out, ALUOp_2_0[0]);
  and and_8 (and_8_out, not_19_out, not_20_out);
  not not_20 (not_20_out, Funct_5_0[2]);
  not not_21 (not_21_out, ALUOp_2_0[0]);
  and and_9 (and_9_out, not_21_out, Funct_5_0[1]);
  not not_22 (not_22_out, ALUOp_2_0[0]);
  and and_10 (and_10_out, not_22_out, not_23_out, Funct_5_0[3]);
  not not_23 (not_23_out, Funct_5_0[4]);
  not not_24 (not_24_out, ALUOp_2_0[0]);
  and and_11 (and_11_out, not_24_out, Funct_5_0[4], not_25_out);
  not not_25 (not_25_out, Funct_5_0[3]);
  not not_26 (not_26_out, ALUOp_2_0[0]);
  not not_27 (not_27_out, Funct_5_0[5]);
  not not_28 (not_28_out, ALUOp_2_0[0]);
  not not_29 (not_29_out, ALUOp_2_0[0]);
  not not_30 (not_30_out, ALUOp_2_0[0]);
  not not_31 (not_31_out, Funct_5_0[4]);
  not not_32 (not_32_out, ALUOp_2_0[0]);
  not not_33 (not_33_out, Funct_5_0[3]);
  not not_34 (not_34_out, ALUOp_2_0[0]);
  not not_35 (not_35_out, Funct_5_0[2]);
  and and_12 (and_12_out, not_4_out, ALUOp_2_0[0]);
  and and_13 (and_13_out, ALUOp_2_0[1], not_5_out, not_6_out);
  and and_14 (and_14_out, ALUOp_2_0[1], not_7_out, not_8_out, Funct_5_0[0]);
  and and_15 (and_15_out, ALUOp_2_0[1], not_9_out, Funct_5_0[1]);
  and and_16 (and_16_out, ALUOp_2_0[1], not_10_out, not_11_out, Funct_5_0[3]);
  and and_17 (and_17_out, ALUOp_2_0[1], not_12_out, Funct_5_0[4], not_13_out);
  and and_18 (and_18_out, ALUOp_2_0[1], not_14_out, Funct_5_0[4], not_15_out);
  and and_19 (and_19_out, ALUOp_2_0[1], not_26_out, not_27_out);
  and and_20 (and_20_out, ALUOp_2_0[1], not_28_out, Funct_5_0[0]);
  and and_21 (and_21_out, ALUOp_2_0[1], not_29_out, Funct_5_0[2], Funct_5_0[1]);
  and and_22 (and_22_out, ALUOp_2_0[1], not_30_out, not_31_out, Funct_5_0[3]);
  and and_23 (and_23_out, ALUOp_2_0[1], not_32_out, Funct_5_0[4], not_33_out);
  and and_24 (and_24_out, ALUOp_2_0[1], not_34_out, Funct_5_0[4], not_35_out);
  or or_1 (ALUCtrl_3_0[3], and_1_out, and_2_out, and_3_out, and_4_out, and_5_out, and_6_out, ALUOp_2_0[2]);
  or or_2 (ALUCtrl_3_0[2], and_12_out, and_13_out, and_14_out, and_15_out, and_16_out, and_17_out, and_18_out, ALUOp_2_0[2]);
  or or_3 (ALUCtrl_3_0[1], not_16_out, and_7_out, and_8_out, and_9_out, and_10_out, and_11_out, ALUOp_2_0[2]);
  or or_4 (ALUCtrl_3_0[0], and_19_out, and_20_out, and_21_out, and_22_out, and_23_out, and_24_out, ALUOp_2_0[2]);
endmodule
