// Logisim project Average.circ as structural Verilog: 1 circuit, main circuit Average
module Average (
  input  [31:0] in_1,
  input  [31:0] in_2,
  output [31:0] out_3
);

  wire [31:0] adder_1_out;

  Adder #(.width(32)) adder_1 (.a(in_1), .b(in_2), .out(adder_1_out));  // open: cin, cout
  Shifter #(.width(32), .shift("ar")) shifter_1 (.in(adder_1_out), .\dist (5'b00001), .out(out_3));
endmodule
