// Logisim project BHT.circ as structural Verilog: 1 circuit, main circuit BHT
module BHT (
  input  Branch,
  input  CLK,
  input  A,
  output out_4
);

  wire and_1_out, and_2_out, and_3_out, and_4_out, and_5_out, and_6_out, and_7_out, and_8_out, not_1_out,
       not_2_out, not_3_out, not_4_out, not_5_out, not_6_out, not_8_out, or_1_out, or_2_out, register_1_q,
       register_2_q;

  not not_1 (not_1_out, A);
  not not_2 (not_2_out, A);
  not not_3 (not_3_out, register_2_q);
  not not_4 (not_4_out, A);
  not not_5 (not_5_out, register_2_q);
  not not_6 (not_6_out, A);
  and and_1 (and_1_out, register_2_q, not_1_out);
  or or_1 (or_1_out, and_1_out, and_2_out, and_3_out);
  and and_2 (and_2_out, register_1_q, not_2_out);
  and and_3 (and_3_out, register_1_q, register_2_q);
  and and_4 (and_4_out, not_3_out, not_4_out);
  and and_5 (and_5_out, register_1_q, not_5_out);
  or or_2 (or_2_out, and_4_out, and_5_out, and_6_out);
  and and_6 (and_6_out, register_1_q, not_6_out);
  and and_7 (and_7_out, Branch, CLK);
  and and_8 (and_8_out, Branch, CLK);
  Register #(.width(1), .trigger("falling")) register_1 (
    .D(or_1_out), .Q(register_1_q), .clk(and_7_out));  // open: en, clr
  Register #(.width(1), .trigger("falling")) register_2 (
    .D(or_2_out), .Q(register_2_q), .clk(and_8_out));  // open: en, clr
  not not_7 (out_4, register_1_q);
  not not_8 (not_8_out, register_2_q);
  // Probe on not_8_out

  // Notes on the sheet:
  //   S'1
  //   S'0
endmodule
