// Logisim project BTB.circ as structural Verilog: 1 circuit, main circuit BTB
module BTB (
  input  [31:0] Current_PC,
  input  [31:0] Previous_PC,
  input  [31:0] TargetedAddr,
  input  EN,
  input  Branched,
  input  CLK,
  input  in_7,
  output [31:0] TargetAddr,
  output Hit
);

  wire comparator_1_eq;
  wire [30:0] multiplexer_2_out;
  wire [31:0] bit_extender_1_out, multiplexer_1_out, ram_1_data;
  wire [31:31] and_1_out;

  and and_1 (and_1_out[31], EN, Branched);
  Multiplexer #(.width(32)) multiplexer_1 (
    .in0(Current_PC), .in1(Previous_PC), .out(multiplexer_1_out), .sel(and_1_out[31]));  // open: en
  RAM #(.addrWidth(24), .dataWidth(32), .bus("separate")) ram_1 (
    .addr(multiplexer_1_out[25:2]), .din({and_1_out[31], TargetedAddr[30:0]}), .data(ram_1_data),
    .str(and_1_out[31]), .clk(CLK), .ld(in_7));  // open: sel, clr
  Multiplexer #(.width(32)) multiplexer_2 (
    .in0({32{1'b0}}), .in1(ram_1_data), .out({Hit, multiplexer_2_out}), .sel(in_7));  // open: en
  assign bit_extender_1_out = {{31{comparator_1_eq}}, comparator_1_eq};  // Bit_Extender bit_extender_1
  Comparator #(.width(5)) comparator_1 (
    .a(multiplexer_1_out[30:26]), .b(multiplexer_2_out[30:26]), .eq(comparator_1_eq));  // open: gt, lt
  assign TargetAddr = bit_extender_1_out & {Hit, multiplexer_2_out};  // AND_Gate and_2, 32 bits wide
endmodule
