// Logisim project BTH.circ as structural Verilog: 1 circuit, main circuit BHT
module BHT (
  input  Branch,
  input  A,
  output out_3
);

  wire and_1_out, and_2_out, and_3_out, and_4_out, and_5_out, and_6_out, not_1_out, not_2_out, or_1_out,
       or_2_out, register_2_q;

  and and_1 (and_1_out, register_2_q, A);
  and and_2 (and_2_out, out_3, A);
  and and_3 (and_3_out, out_3, register_2_q);
  not not_1 (not_1_out, register_2_q);
  not not_2 (not_2_out, register_2_q);
  or or_1 (or_1_out, and_1_out, and_2_out, and_3_out);
  and and_4 (and_4_out, not_1_out, A);
  and and_5 (and_5_out, out_3, not_2_out);
  and and_6 (and_6_out, out_3, A);
  Register #(.width(1)) register_1 (.D(or_1_out), .Q(out_3), .clk(Branch));  // open: en, clr
  Register #(.width(1)) register_2 (.D(or_2_out), .Q(register_2_q), .clk(Branch));  // open: en, clr
  or or_2 (or_2_out, and_4_out, and_5_out, and_6_out);

  // Notes on the sheet:
  //   S'1
  //   S'0
endmodule
