// Logisim project ControlUnit.circ as structural Verilog: 3 circuits, main circuit ControlUnit
// Control Unit
module ControlUnit (
  input  [5:0] in_1,
  input  [5:0] in_2,
  output out_3,
  output out_4,
  output out_5,
  output out_6,
  output out_7,
  output out_8,
  output out_9,
  output out_10,
  output [3:0] out_11
);

  wire main_decoder_1_error;
  wire [2:0] main_decoder_1_aluop_2_0;

  not not_1 (out_3, main_decoder_1_error);
  Main_Decoder main_decoder_1 (
    .Op_5_0(in_1), .MemtoReg(out_5), .MemWrite(out_6), .Branch(out_7), .ALUSrc(out_8), .RegDst(out_9),
    .RegWrite(out_10), .Jump(out_4), .ALUOp_2_0(main_decoder_1_aluop_2_0), .Error(main_decoder_1_error));
  ALU_Decoder alu_decoder_1 (.ALUOp_2_0(main_decoder_1_aluop_2_0), .Funct_5_0(in_2), .ALUCtrl_3_0(out_11));
endmodule

module Main_Decoder (
  input  [5:0] Op_5_0,
  output MemtoReg,
  output MemWrite,
  output Branch,
  output ALUSrc,
  output RegDst,
  output RegWrite,
  output Jump,
  output [2:0] ALUOp_2_0,
  output Error
);

  wire and_1_out, and_2_out, and_6_out, and_7_out, and_8_out, and_10_out, and_11_out, and_12_out, and_13_out,
       and_14_out, and_15_out, and_16_out, and_17_out, and_18_out, and_19_out, and_20_out, and_21_out,
       and_22_out, and_23_out, and_24_out, and_25_out, and_26_out, and_27_out, and_28_out, and_29_out,
       and_30_out, and_31_out, and_32_out, and_33_out, and_34_out, not_1_out, not_2_out, not_3_out,
       not_4_out, not_5_out, not_6_out, not_7_out, not_8_out, not_9_out, not_10_out, not_11_out, not_12_out,
       not_13_out, not_14_out, not_15_out, not_16_out, not_17_out, not_18_out, not_19_out, not_20_out,
       not_21_out, not_22_out, not_23_out, not_24_out, not_25_out, not_26_out, not_27_out, not_28_out,
       not_29_out, not_30_out, not_31_out, not_32_out, not_33_out, not_34_out, not_35_out, not_36_out,
       not_37_out, not_38_out, not_39_out, not_40_out, not_41_out, not_42_out, not_43_out, not_44_out,
       not_45_out, not_46_out, not_47_out, not_48_out, not_49_out;

  not not_1 (not_1_out, Op_5_0[5]);
  not not_2 (not_2_out, Op_5_0[4]);
  not not_3 (not_3_out, Op_5_0[3]);
  not not_4 (not_4_out, Op_5_0[2]);
  not not_5 (not_5_out, Op_5_0[1]);
  not not_6 (not_6_out, Op_5_0[4]);
  not not_7 (not_7_out, Op_5_0[2]);
  not not_8 (not_8_out, Op_5_0[4]);
  not not_9 (not_9_out, Op_5_0[2]);
  not not_10 (not_10_out, Op_5_0[3]);
  or or_1 (ALUSrc, Op_5_0[1], Op_5_0[3]);
  not not_11 (not_11_out, Op_5_0[3]);
  not not_12 (not_12_out, Op_5_0[1]);
  not not_13 (not_13_out, Op_5_0[5]);
  not not_14 (not_14_out, Op_5_0[4]);
  not not_15 (not_15_out, Op_5_0[2]);
  not not_16 (not_16_out, Op_5_0[1]);
  not not_17 (not_17_out, Op_5_0[0]);
  not not_18 (not_18_out, Op_5_0[4]);
  not not_19 (not_19_out, Op_5_0[3]);
  not not_20 (not_20_out, Op_5_0[2]);
  not not_21 (not_21_out, Op_5_0[1]);
  not not_22 (not_22_out, Op_5_0[0]);
  not not_23 (not_23_out, Op_5_0[0]);
  not not_24 (not_24_out, Op_5_0[1]);
  not not_25 (not_25_out, Op_5_0[5]);
  not not_26 (not_26_out, Op_5_0[5]);
  not not_27 (not_27_out, Op_5_0[3]);
  not not_28 (not_28_out, Op_5_0[2]);
  not not_29 (not_29_out, Op_5_0[4]);
  not not_30 (not_30_out, Op_5_0[0]);
  not not_31 (not_31_out, Op_5_0[3]);
  not not_32 (not_32_out, Op_5_0[2]);
  not not_33 (not_33_out, Op_5_0[1]);
  not not_34 (not_34_out, Op_5_0[5]);
  not not_35 (not_35_out, Op_5_0[0]);
  not not_36 (not_36_out, Op_5_0[1]);
  not not_37 (not_37_out, Op_5_0[5]);
  not not_38 (not_38_out, Op_5_0[0]);
  not not_39 (not_39_out, Op_5_0[1]);
  not not_40 (not_40_out, Op_5_0[5]);
  not not_41 (not_41_out, Op_5_0[1]);
  not not_42 (not_42_out, Op_5_0[0]);
  not not_43 (not_43_out, Op_5_0[5]);
  not not_44 (not_44_out, Op_5_0[3]);
  not not_45 (not_45_out, Op_5_0[2]);
  not not_46 (not_46_out, Op_5_0[4]);
  not not_47 (not_47_out, Op_5_0[1]);
  not not_48 (not_48_out, Op_5_0[4]);
  not not_49 (not_49_out, Op_5_0[0]);
  and and_1 (and_1_out, not_1_out, not_2_out, not_3_out, not_4_out, not_5_out, Op_5_0[0]);
  and and_2 (and_2_out, Op_5_0[5], not_6_out, not_7_out, Op_5_0[1], Op_5_0[0]);
  and and_3 (MemWrite, Op_5_0[5], not_8_out, Op_5_0[3], not_9_out, Op_5_0[1], Op_5_0[0]);
  and and_4 (Branch, not_10_out, Op_5_0[2]);
  and and_5 (RegDst, not_11_out, not_12_out);
  and and_6 (and_6_out, not_13_out, not_14_out, not_15_out, not_16_out, not_17_out);
  and and_7 (and_7_out, Op_5_0[5], not_18_out, not_19_out, not_20_out, Op_5_0[1], Op_5_0[0]);
  and and_8 (and_8_out, Op_5_0[5], Op_5_0[4], Op_5_0[3], Op_5_0[2], not_21_out, not_22_out);
  and and_9 (Jump, Op_5_0[1], not_23_out);
  and and_10 (and_10_out, not_24_out, Op_5_0[0]);
  and and_11 (and_11_out, not_25_out, Op_5_0[1]);
  and and_12 (and_12_out, Op_5_0[2], Op_5_0[1]);
  and and_13 (and_13_out, not_26_out, Op_5_0[3], Op_5_0[2]);
  and and_14 (and_14_out, Op_5_0[4], not_27_out);
  and and_15 (and_15_out, Op_5_0[4], not_28_out);
  and and_16 (and_16_out, Op_5_0[5], not_29_out, not_30_out);
  and and_17 (and_17_out, not_31_out, not_32_out, not_33_out);
  and and_18 (and_18_out, not_34_out, Op_5_0[0]);
  and and_19 (and_19_out, Op_5_0[1], not_35_out);
  and and_20 (and_20_out, Op_5_0[3], Op_5_0[2]);
  and and_21 (and_21_out, Op_5_0[5], not_36_out);
  and and_22 (and_22_out, Op_5_0[5], Op_5_0[2]);
  and and_23 (and_23_out, not_37_out, Op_5_0[0]);
  and and_24 (and_24_out, Op_5_0[1], not_38_out);
  and and_25 (and_25_out, Op_5_0[5], not_39_out);
  and and_26 (and_26_out, not_40_out, Op_5_0[0]);
  and and_27 (and_27_out, not_41_out, Op_5_0[0]);
  and and_28 (and_28_out, Op_5_0[2], Op_5_0[1]);
  and and_29 (and_29_out, Op_5_0[3], Op_5_0[1], not_42_out);
  and and_30 (and_30_out, not_43_out, Op_5_0[3], Op_5_0[2]);
  and and_31 (and_31_out, Op_5_0[4], not_44_out);
  and and_32 (and_32_out, Op_5_0[4], not_45_out);
  and and_33 (and_33_out, Op_5_0[5], not_46_out, not_47_out);
  and and_34 (and_34_out, Op_5_0[5], not_48_out, not_49_out);
  or or_2 (MemtoReg, and_1_out, and_2_out);
  or or_3 (RegWrite, and_6_out, and_7_out, and_8_out);
  or or_4 (ALUOp_2_0[2], and_10_out, and_11_out, and_12_out, and_13_out, and_14_out, and_15_out, and_16_out);
  or or_5 (ALUOp_2_0[1], and_17_out, and_18_out, and_19_out, and_20_out, Op_5_0[4], and_21_out, and_22_out);
  or or_6 (ALUOp_2_0[0], and_23_out, and_24_out, Op_5_0[2], Op_5_0[4], and_25_out);
  or or_7 (Error, and_26_out, and_27_out, and_28_out, and_29_out, and_30_out, and_31_out, and_32_out, and_33_out, and_34_out);
endmodule

module ALU_Decoder (
  input  [2:0] ALUOp_2_0,
  input  [5:0] Funct_5_0,
  output [3:0] ALUCtrl_3_0
);

  wire and_1_out, and_2_out, and_3_out, and_4_out, and_5_out, and_6_out, and_7_out, and_8_out, and_9_out,
       and_10_out, and_11_out, and_12_out, and_13_out, and_14_out, and_15_out, and_16_out, and_17_out,
       and_18_out, and_19_out, and_20_out, and_21_out, and_22_out, and_23_out, and_24_out, not_1_out,
       not_2_out, not_3_out, not_4_out, not_5_out, not_6_out, not_7_out, not_8_out, not_9_out, not_10_out,
       not_11_out, not_12_out, not_13_out, not_14_out, not_15_out, not_16_out, not_17_out, not_18_out,
       not_19_out, not_20_out, not_21_out, not_22_out, not_23_out, not_24_out, not_25_out, not_26_out,
       not_27_out, not_28_out, not_29_out, not_30_out, not_31_out, not_32_out, not_33_out, not_34_out,
       not_35_out;

  not not_1 (not_1_out, Funct_5_0[5]);
  not not_2 (not_2_out, Funct_5_0[2]);
  not not_3 (not_3_out, Funct_5_0[1]);
  not not_4 (not_4_out, ALUOp_2_0[1]);
  not not_5 (not_5_out, ALUOp_2_0[0]);
  not not_6 (not_6_out, Funct_5_0[5]);
  not not_7 (not_7_out, ALUOp_2_0[0]);
  not not_8 (not_8_out, Funct_5_0[2]);
  not not_9 (not_9_out, ALUOp_2_0[0]);
  not not_10 (not_10_out, ALUOp_2_0[0]);
  not not_11 (not_11_out, Funct_5_0[4]);
  not not_12 (not_12_out, ALUOp_2_0[0]);
  not not_13 (not_13_out, Funct_5_0[3]);
  not not_14 (not_14_out, ALUOp_2_0[0]);
  not not_15 (not_15_out, Funct_5_0[2]);
  not not_16 (not_16_out, ALUOp_2_0[0]);
  not not_17 (not_17_out, Funct_5_0[5]);
  not not_18 (not_18_out, ALUOp_2_0[0]);
  not not_19 (not_19_out, Funct_5_0[2]);
  not not_20 (not_20_out, ALUOp_2_0[0]);
  not not_21 (not_21_out, ALUOp_2_0[0]);
  not not_22 (not_22_out, Funct_5_0[4]);
  not not_23 (not_23_out, ALUOp_2_0[0]);
  not not_24 (not_24_out, Funct_5_0[3]);
  not not_25 (not_25_out, ALUOp_2_0[0]);
  not not_26 (not_26_out, Funct_5_0[5]);
  not not_27 (not_27_out, ALUOp_2_0[0]);
  not not_28 (not_28_out, ALUOp_2_0[0]);
  not not_29 (not_29_out, ALUOp_2_0[0]);
  not not_30 (not_30_out, Funct_5_0[4]);
  not not_31 (not_31_out, ALUOp_2_0[0]);
  not not_32 (not_32_out, Funct_5_0[3]);
  not not_33 (not_33_out, ALUOp_2_0[0]);
  not not_34 (not_34_out, Funct_5_0[2]);
  and and_1 (and_1_out, ALUOp_2_0[1], not_1_out);
  and and_2 (and_2_out, ALUOp_2_0[1], not_2_out, Funct_5_0[0]);
  and and_3 (and_3_out, ALUOp_2_0[1], Funct_5_0[2], Funct_5_0[1]);
  and and_4 (and_4_out, ALUOp_2_0[1], Funct_5_0[3], not_3_out);
  and and_5 (and_5_out, ALUOp_2_0[1], Funct_5_0[4]);
  and and_6 (and_6_out, ALUOp_2_0[1], ALUOp_2_0[0]);
  and and_7 (and_7_out, not_4_out, ALUOp_2_0[0]);
  and and_8 (and_8_out, ALUOp_2_0[1], not_5_out, not_6_out);
  and and_9 (and_9_out, ALUOp_2_0[1], not_7_out, not_8_out, Funct_5_0[0]);
  and and_10 (and_10_out, ALUOp_2_0[1], not_9_out, Funct_5_0[1]);
  and and_11 (and_11_out, ALUOp_2_0[1], not_10_out, not_11_out, Funct_5_0[3]);
  and and_12 (and_12_out, ALUOp_2_0[1], not_12_out, Funct_5_0[4], not_13_out);
  and and_13 (and_13_out, ALUOp_2_0[1], not_14_out, Funct_5_0[4], not_15_out);
  not not_35 (not_35_out, ALUOp_2_0[1]);
  and and_14 (and_14_out, not_16_out, not_17_out);
  and and_15 (and_15_out, not_18_out, not_19_out);
  and and_16 (and_16_out, not_20_out, Funct_5_0[1]);
  and and_17 (and_17_out, not_21_out, not_22_out, Funct_5_0[3]);
  and and_18 (and_18_out, not_23_out, Funct_5_0[4], not_24_out);
  and and_19 (and_19_out, ALUOp_2_0[1], not_25_out, not_26_out);
  and and_20 (and_20_out, ALUOp_2_0[1], not_27_out, Funct_5_0[0]);
  and and_21 (and_21_out, ALUOp_2_0[1], not_28_out, Funct_5_0[2], Funct_5_0[1]);
  and and_22 (and_22_out, ALUOp_2_0[1], not_29_out, not_30_out, Funct_5_0[3]);
  and and_23 (and_23_out, ALUOp_2_0[1], not_31_out, Funct_5_0[4], not_32_out);
  and and_24 (and_24_out, ALUOp_2_0[1], not_33_out, Funct_5_0[4], not_34_out);
  or or_1 (ALUCtrl_3_0[3], and_1_out, and_2_out, and_3_out, and_4_out, and_5_out, and_6_out, ALUOp_2_0[2]);
  or or_2 (ALUCtrl_3_0[2], and_7_out, and_8_out, and_9_out, and_10_out, and_11_out, and_12_out, and_13_out, ALUOp_2_0[2]);
  or or_3 (ALUCtrl_3_0[1], not_35_out, and_14_out, and_15_out, and_16_out, and_17_out, and_18_out, ALUOp_2_0[2]);
  or or_4 (ALUCtrl_3_0[0], and_19_out, and_20_out, and_21_out, and_22_out, and_23_out, and_24_out, ALUOp_2_0[2]);
endmodule
