// Logisim project DataMem.circ as structural Verilog: 1 circuit, main circuit Data Mem
module Data_Mem (
  input  [31:0] A,
  input  CLK,
  input  WE,
  input  [31:0] WD,
  output [31:0] RD
);

  wire not_1_out;

  not not_1 (not_1_out, WE);
  RAM #(.dataWidth(32)) ram_1 (.addr(A[7:0]), .data(RD), .clk(CLK), .ld(not_1_out));  // open: sel, clr
  assign RD = WE ? WD : 32'bz;  // Controlled_Buffer controlled_buffer_1
endmodule
