// Logisim project Forwarding_Unit.circ as structural Verilog: 1 circuit, main circuit Forwarding_Unit
module Forwarding_Unit (
  input  RegWrite_EX_MEM,
  input  RegWrite_MEM_WB,
  input  [4:0] ID_EX_RegRs,
  input  [4:0] EX_MEM_RegRd,
  input  [4:0] ID_EX_RegRt,
  input  [4:0] MEM_WB_RegRd,
  output [1:0] MUX_A,
  output [1:0] MUX_B
);

  wire comparator_1_eq, comparator_2_eq, comparator_3_eq, comparator_4_eq, not_1_out, not_2_out, not_3_out,
       not_4_out, or_1_out;

  or or_1 (or_1_out, RegWrite_EX_MEM, RegWrite_MEM_WB);
  Comparator #(.width(5)) comparator_1 (.a(ID_EX_RegRs), .b(EX_MEM_RegRd), .eq(comparator_1_eq));  // open: gt, lt
  Comparator #(.width(5)) comparator_2 (.a(EX_MEM_RegRd), .b(ID_EX_RegRt), .eq(comparator_2_eq));  // open: gt, lt
  Comparator #(.width(5)) comparator_3 (.a(ID_EX_RegRs), .b(MEM_WB_RegRd), .eq(comparator_3_eq));  // open: gt, lt
  Comparator #(.width(5)) comparator_4 (.a(MEM_WB_RegRd), .b(ID_EX_RegRt), .eq(comparator_4_eq));  // open: gt, lt
  not not_1 (not_1_out, comparator_1_eq);
  not not_2 (not_2_out, comparator_2_eq);
  and and_1 (MUX_A[0], or_1_out, comparator_1_eq);
  not not_3 (not_3_out, comparator_1_eq);
  not not_4 (not_4_out, comparator_2_eq);
  and and_2 (MUX_B[0], or_1_out, comparator_2_eq);
  and and_3 (MUX_A[1], or_1_out, not_1_out, not_2_out, comparator_3_eq);
  and and_4 (MUX_B[1], or_1_out, not_3_out, not_4_out, comparator_4_eq);

  // Notes on the sheet:
  //   RegWrite_MEM_WB: pull=up
  //   No Hazard X -> MUX : 00
  //   EX_Hazard -> MUX : 01
  //   MEM_Hazard -> MUX : 10
  //   ALU_A
  //   ALU_B
  //   ALU_A
  //   ALU_B
endmodule
