// Logisim project Hazard_Detect.circ as structural Verilog: 1 circuit, main circuit Hazard_Detect
module Hazard_Detect (
  input  in_1,
  input  [4:0] in_2,
  input  [4:0] in_3,
  input  CLK,
  input  [4:0] in_5,
  output out_6,
  output out_7,
  output out_8
);

  wire and_1_out, comparator_1_eq, comparator_2_eq, d_ff_1_q, or_1_out;

  Comparator #(.width(5)) comparator_1 (.a(in_2), .b(in_3), .eq(comparator_1_eq));  // open: gt, lt
  Comparator #(.width(5)) comparator_2 (.a(in_3), .b(in_5), .eq(comparator_2_eq));  // open: gt, lt
  or or_1 (or_1_out, comparator_1_eq, comparator_2_eq);
  and and_1 (and_1_out, in_1, or_1_out);
  not not_1 (out_6, and_1_out);
  not not_2 (out_7, and_1_out);
  D_Flip_Flop #(.trigger("falling")) d_ff_1 (.clk(CLK), .D(and_1_out), .Q(d_ff_1_q));  // open: Qn, preset, en, reset
  and and_2 (out_8, CLK, d_ff_1_q);
endmodule
