// Logisim project Hazard_Stall.circ as structural Verilog: 2 circuits, main circuit Ctrl_Hazard_Stall
module Ctrl_Hazard_Stall (
  input  RegWriteE,
  input  [4:0] rsD,
  input  [4:0] WriteRegE,
  input  [4:0] rtD,
  input  BranchD,
  input  [4:0] WriteRegM,
  input  MemtoRegM,
  output BranchStall
);

  wire and_1_out, and_2_out, comparator_1_eq, comparator_2_eq, comparator_3_eq, comparator_4_eq, or_1_out,
       or_2_out;

  Comparator #(.width(5)) comparator_1 (.a(rsD), .b(WriteRegE), .eq(comparator_1_eq));  // open: gt, lt
  Comparator #(.width(5)) comparator_2 (.a(WriteRegE), .b(rtD), .eq(comparator_2_eq));  // open: gt, lt
  Comparator #(.width(5)) comparator_3 (.a(rtD), .b(WriteRegM), .eq(comparator_3_eq));  // open: gt, lt
  Comparator #(.width(5)) comparator_4 (.a(WriteRegM), .b(rsD), .eq(comparator_4_eq));  // open: gt, lt
  or or_1 (or_1_out, comparator_1_eq, comparator_2_eq);
  or or_2 (or_2_out, comparator_3_eq, comparator_4_eq);
  and and_1 (and_1_out, RegWriteE, or_1_out, BranchD);
  and and_2 (and_2_out, BranchD, or_2_out, MemtoRegM);
  or or_3 (BranchStall, and_1_out, and_2_out);
endmodule

module Data_Hazard_Stall (
  input  MemWriteD,
  input  MemtoRegE,
  input  RegWriteE,
  input  [4:0] rsD,
  input  [4:0] rtE,
  input  [4:0] rtD,
  output lwstall
);

  wire comparator_1_eq, comparator_2_eq, not_1_out, or_1_out;

  not not_1 (not_1_out, MemWriteD);
  Comparator #(.width(5)) comparator_1 (.a(rsD), .b(rtE), .eq(comparator_1_eq));  // open: gt, lt
  Comparator #(.width(5)) comparator_2 (.a(rtE), .b(rtD), .eq(comparator_2_eq));  // open: gt, lt
  or or_1 (or_1_out, comparator_1_eq, comparator_2_eq);
  and and_1 (lwstall, not_1_out, MemtoRegE, RegWriteE, or_1_out);
endmodule
