// Logisim project Hazard_Unit.circ as structural Verilog: 1 circuit, main circuit Hazard_Unit
module Hazard_Unit (
  input  CLK,
  input  BranchD,
  input  RegWriteE,
  input  RegWriteM,
  input  RegWriteW,
  input  MemWriteD,
  input  MemWriteE,
  input  MemtoRegM,
  input  MemtoRegE,
  input  [4:0] RsD,
  input  [4:0] RsE,
  input  [4:0] RtD,
  input  [4:0] RtE,
  input  [4:0] WriteRegM,
  input  [4:0] WriteRegW,
  input  [4:0] WriteRegE,
  output StallF,
  output StallD,
  output FlushE,
  output [1:0] ForwardAE,
  output [1:0] ForwardBE,
  output ForwardM,
  output ForwardAD,
  output ForwardBD
);

  wire ctrl_hazard_stall_1_branchstall, d_ff_1_q, data_hazard_stall_1_lwstall, or_1_out;

  Data_Hazard_Stall data_hazard_stall_1 (
    .MemtoRegE(MemtoRegE), .rsD(RsD), .rtE(RtE), .rtD(RtD), .lwstall(data_hazard_stall_1_lwstall),
    .MemWriteD(MemWriteD), .RegWriteE(RegWriteE));
  Ctrl_Hazard_Stall ctrl_hazard_stall_1 (
    .RegWriteE(RegWriteE), .rsD(RsD), .WriteRegE(WriteRegE), .rtD(RtD), .BranchD(BranchD),
    .WriteRegM(WriteRegM), .MemtoRegM(MemtoRegM), .BranchStall(ctrl_hazard_stall_1_branchstall));
  Data_Hazard_Forwarding data_hazard_forwarding_1 (
    .RegWriteM(RegWriteM), .MUX_A(ForwardAE), .EX_MEM_RegRd(WriteRegM), .ID_EX_RegRs(RsE), .ID_EX_RegRt(RtE),
    .MEM_WB_RegRd(WriteRegW), .MUX_B(ForwardBE), .RegWriteW(RegWriteW), .out_10(ForwardM),
    .MemWriteE(MemWriteE));
  Ctrl_Hazard_Forwarding ctrl_hazard_forwarding_1 (
    .RsD(RsD), .RdM(WriteRegM), .RegWriteM(RegWriteM), .RtD(RtD), .ForwardAD(ForwardAD), .ForwardBD(ForwardBD));
  or or_1 (or_1_out, data_hazard_stall_1_lwstall, ctrl_hazard_stall_1_branchstall);
  D_Flip_Flop #(.trigger("falling")) d_ff_1 (.clk(CLK), .D(or_1_out), .Q(d_ff_1_q));  // open: Qn, preset, en, reset
  not not_1 (StallF, or_1_out);
  not not_2 (StallD, or_1_out);
  and and_1 (FlushE, CLK, d_ff_1_q);

  // Other names for the same wires on the sheet: RdE[4:0] = WriteRegE; RdM[4:0] = WriteRegM; RdW[4:0] = WriteRegW

  // Notes on the sheet:
  //   ForwardAE: pull=up
  //   ForwardBE: pull=up
endmodule
