// Logisim project InstMem.circ as structural Verilog: 1 circuit, main circuit InstMem
module InstMem (
  input  [31:0] A,
  output [31:0] out_2
);

  wire [23:0] demultiplexer_1_out0, demultiplexer_1_out1, demultiplexer_1_out2, demultiplexer_1_out3,
       demultiplexer_1_out4, demultiplexer_1_out5, demultiplexer_1_out6, demultiplexer_1_out7,
       demultiplexer_1_out8, demultiplexer_1_out9, demultiplexer_1_out10, demultiplexer_1_out11,
       demultiplexer_1_out12, demultiplexer_1_out13, demultiplexer_1_out14, demultiplexer_1_out15,
       demultiplexer_1_out16, demultiplexer_1_out17, demultiplexer_1_out18, demultiplexer_1_out19,
       demultiplexer_1_out20, demultiplexer_1_out21, demultiplexer_1_out22, demultiplexer_1_out23,
       demultiplexer_1_out24, demultiplexer_1_out25, demultiplexer_1_out26, demultiplexer_1_out27,
       demultiplexer_1_out28, demultiplexer_1_out29, demultiplexer_1_out30, demultiplexer_1_out31,
       demultiplexer_2_out0, demultiplexer_2_out1, demultiplexer_3_out0, demultiplexer_3_out1,
       demultiplexer_3_out2, demultiplexer_3_out3, demultiplexer_3_out4, demultiplexer_3_out5,
       demultiplexer_3_out6, demultiplexer_3_out7, demultiplexer_3_out8, demultiplexer_3_out9,
       demultiplexer_3_out10, demultiplexer_3_out11, demultiplexer_3_out12, demultiplexer_3_out13,
       demultiplexer_3_out14, demultiplexer_3_out15, demultiplexer_3_out16, demultiplexer_3_out17,
       demultiplexer_3_out18, demultiplexer_3_out19, demultiplexer_3_out20, demultiplexer_3_out21,
       demultiplexer_3_out22, demultiplexer_3_out23, demultiplexer_3_out24, demultiplexer_3_out25,
       demultiplexer_3_out26, demultiplexer_3_out27, demultiplexer_3_out28, demultiplexer_3_out29,
       demultiplexer_3_out30, demultiplexer_3_out31;
  wire [31:0] multiplexer_1_out, multiplexer_2_out, rom_1_data, rom_2_data, rom_3_data, rom_4_data,
       rom_5_data, rom_6_data, rom_7_data, rom_8_data, rom_9_data, rom_10_data, rom_11_data, rom_12_data,
       rom_13_data, rom_14_data, rom_15_data, rom_16_data, rom_17_data, rom_18_data, rom_19_data,
       rom_20_data, rom_21_data, rom_22_data, rom_23_data, rom_24_data, rom_25_data, rom_26_data,
       rom_27_data, rom_28_data, rom_29_data, rom_30_data, rom_31_data, rom_32_data, rom_33_data,
       rom_34_data, rom_35_data, rom_36_data, rom_37_data, rom_38_data, rom_39_data, rom_40_data,
       rom_41_data, rom_42_data, rom_43_data, rom_44_data, rom_45_data, rom_46_data, rom_47_data,
       rom_48_data, rom_49_data, rom_50_data, rom_51_data, rom_52_data, rom_53_data, rom_54_data,
       rom_55_data, rom_56_data, rom_57_data, rom_58_data, rom_59_data, rom_60_data, rom_61_data,
       rom_62_data, rom_63_data, rom_64_data;

  Demultiplexer #(.select(5), .width(24)) demultiplexer_1 (
    .out0(demultiplexer_1_out0), .out1(demultiplexer_1_out1), .out2(demultiplexer_1_out2),
    .out3(demultiplexer_1_out3), .out4(demultiplexer_1_out4), .out5(demultiplexer_1_out5),
    .out6(demultiplexer_1_out6), .out7(demultiplexer_1_out7), .out8(demultiplexer_1_out8),
    .out9(demultiplexer_1_out9), .out10(demultiplexer_1_out10), .out11(demultiplexer_1_out11),
    .out12(demultiplexer_1_out12), .out13(demultiplexer_1_out13), .out14(demultiplexer_1_out14),
    .out15(demultiplexer_1_out15), .out16(demultiplexer_1_out16), .out17(demultiplexer_1_out17),
    .out18(demultiplexer_1_out18), .out19(demultiplexer_1_out19), .out20(demultiplexer_1_out20),
    .out21(demultiplexer_1_out21), .out22(demultiplexer_1_out22), .out23(demultiplexer_1_out23),
    .out24(demultiplexer_1_out24), .out25(demultiplexer_1_out25), .out26(demultiplexer_1_out26),
    .out27(demultiplexer_1_out27), .out28(demultiplexer_1_out28), .out29(demultiplexer_1_out29),
    .out30(demultiplexer_1_out30), .out31(demultiplexer_1_out31), .in(demultiplexer_2_out0), .sel(A[30:26]));  // open: en
  Demultiplexer #(.width(24)) demultiplexer_2 (
    .out0(demultiplexer_2_out0), .out1(demultiplexer_2_out1), .in(A[25:2]), .sel(A[31]));  // open: en
  Demultiplexer #(.select(5), .width(24)) demultiplexer_3 (
    .out0(demultiplexer_3_out0), .out1(demultiplexer_3_out1), .out2(demultiplexer_3_out2),
    .out3(demultiplexer_3_out3), .out4(demultiplexer_3_out4), .out5(demultiplexer_3_out5),
    .out6(demultiplexer_3_out6), .out7(demultiplexer_3_out7), .out8(demultiplexer_3_out8),
    .out9(demultiplexer_3_out9), .out10(demultiplexer_3_out10), .out11(demultiplexer_3_out11),
    .out12(demultiplexer_3_out12), .out13(demultiplexer_3_out13), .out14(demultiplexer_3_out14),
    .out15(demultiplexer_3_out15), .out16(demultiplexer_3_out16), .out17(demultiplexer_3_out17),
    .out18(demultiplexer_3_out18), .out19(demultiplexer_3_out19), .out20(demultiplexer_3_out20),
    .out21(demultiplexer_3_out21), .out22(demultiplexer_3_out22), .out23(demultiplexer_3_out23),
    .out24(demultiplexer_3_out24), .out25(demultiplexer_3_out25), .out26(demultiplexer_3_out26),
    .out27(demultiplexer_3_out27), .out28(demultiplexer_3_out28), .out29(demultiplexer_3_out29),
    .out30(demultiplexer_3_out30), .out31(demultiplexer_3_out31), .in(demultiplexer_2_out1), .sel(A[30:26]));  // open: en
  ROM #(.addrWidth(24), .dataWidth(32)) rom_1 (.addr(demultiplexer_1_out0), .data(rom_1_data));  // open: sel
  ROM #(.addrWidth(24), .dataWidth(32)) rom_2 (.addr(demultiplexer_1_out1), .data(rom_2_data));  // open: sel
  ROM #(.addrWidth(24), .dataWidth(32)) rom_3 (.addr(demultiplexer_1_out2), .data(rom_3_data));  // open: sel
  ROM #(.addrWidth(24), .dataWidth(32)) rom_4 (.addr(demultiplexer_1_out3), .data(rom_4_data));  // open: sel
  ROM #(.addrWidth(24), .dataWidth(32)) rom_5 (.addr(demultiplexer_1_out4), .data(rom_5_data));  // open: sel
  ROM #(.addrWidth(24), .dataWidth(32)) rom_6 (.addr(demultiplexer_1_out5), .data(rom_6_data));  // open: sel
  ROM #(.addrWidth(24), .dataWidth(32)) rom_7 (.addr(demultiplexer_1_out6), .data(rom_7_data));  // open: sel
  ROM #(.addrWidth(24), .dataWidth(32)) rom_8 (.addr(demultiplexer_1_out7), .data(rom_8_data));  // open: sel
  ROM #(.addrWidth(24), .dataWidth(32)) rom_9 (.addr(demultiplexer_1_out8), .data(rom_9_data));  // open: sel
  ROM #(.addrWidth(24), .dataWidth(32)) rom_10 (.addr(demultiplexer_1_out9), .data(rom_10_data));  // open: sel
  ROM #(.addrWidth(24), .dataWidth(32)) rom_11 (.addr(demultiplexer_1_out10), .data(rom_11_data));  // open: sel
  ROM #(.addrWidth(24), .dataWidth(32)) rom_12 (.addr(demultiplexer_1_out11), .data(rom_12_data));  // open: sel
  ROM #(.addrWidth(24), .dataWidth(32)) rom_13 (.addr(demultiplexer_1_out12), .data(rom_13_data));  // open: sel
  ROM #(.addrWidth(24), .dataWidth(32)) rom_14 (.addr(demultiplexer_1_out13), .data(rom_14_data));  // open: sel
  ROM #(.addrWidth(24), .dataWidth(32)) rom_15 (.addr(demultiplexer_1_out14), .data(rom_15_data));  // open: sel
  ROM #(.addrWidth(24), .dataWidth(32)) rom_16 (.addr(demultiplexer_1_out15), .data(rom_16_data));  // open: sel
  ROM #(.addrWidth(24), .dataWidth(32)) rom_17 (.addr(demultiplexer_1_out16), .data(rom_17_data));  // open: sel
  ROM #(.addrWidth(24), .dataWidth(32)) rom_18 (.addr(demultiplexer_1_out17), .data(rom_18_data));  // open: sel
  ROM #(.addrWidth(24), .dataWidth(32)) rom_19 (.addr(demultiplexer_1_out18), .data(rom_19_data));  // open: sel
  ROM #(.addrWidth(24), .dataWidth(32)) rom_20 (.addr(demultiplexer_1_out19), .data(rom_20_data));  // open: sel
  ROM #(.addrWidth(24), .dataWidth(32)) rom_21 (.addr(demultiplexer_1_out20), .data(rom_21_data));  // open: sel
  ROM #(.addrWidth(24), .dataWidth(32)) rom_22 (.addr(demultiplexer_1_out21), .data(rom_22_data));  // open: sel
  ROM #(.addrWidth(24), .dataWidth(32)) rom_23 (.addr(demultiplexer_1_out22), .data(rom_23_data));  // open: sel
  ROM #(.addrWidth(24), .dataWidth(32)) rom_24 (.addr(demultiplexer_1_out23), .data(rom_24_data));  // open: sel
  ROM #(.addrWidth(24), .dataWidth(32)) rom_25 (.addr(demultiplexer_1_out24), .data(rom_25_data));  // open: sel
  ROM #(.addrWidth(24), .dataWidth(32)) rom_26 (.addr(demultiplexer_1_out25), .data(rom_26_data));  // open: sel
  ROM #(.addrWidth(24), .dataWidth(32)) rom_27 (.addr(demultiplexer_1_out26), .data(rom_27_data));  // open: sel
  ROM #(.addrWidth(24), .dataWidth(32)) rom_28 (.addr(demultiplexer_1_out27), .data(rom_28_data));  // open: sel
  ROM #(.addrWidth(24), .dataWidth(32)) rom_29 (.addr(demultiplexer_1_out28), .data(rom_29_data));  // open: sel
  ROM #(.addrWidth(24), .dataWidth(32)) rom_30 (.addr(demultiplexer_1_out29), .data(rom_30_data));  // open: sel
  ROM #(.addrWidth(24), .dataWidth(32)) rom_31 (.addr(demultiplexer_1_out30), .data(rom_31_data));  // open: sel
  ROM #(.addrWidth(24), .dataWidth(32)) rom_32 (.addr(demultiplexer_1_out31), .data(rom_32_data));  // open: sel
  ROM #(.addrWidth(24), .dataWidth(32)) rom_33 (.addr(demultiplexer_3_out0), .data(rom_33_data));  // open: sel
  ROM #(.addrWidth(24), .dataWidth(32)) rom_34 (.addr(demultiplexer_3_out1), .data(rom_34_data));  // open: sel
  ROM #(.addrWidth(24), .dataWidth(32)) rom_35 (.addr(demultiplexer_3_out2), .data(rom_35_data));  // open: sel
  ROM #(.addrWidth(24), .dataWidth(32)) rom_36 (.addr(demultiplexer_3_out3), .data(rom_36_data));  // open: sel
  ROM #(.addrWidth(24), .dataWidth(32)) rom_37 (.addr(demultiplexer_3_out4), .data(rom_37_data));  // open: sel
  ROM #(.addrWidth(24), .dataWidth(32)) rom_38 (.addr(demultiplexer_3_out5), .data(rom_38_data));  // open: sel
  ROM #(.addrWidth(24), .dataWidth(32)) rom_39 (.addr(demultiplexer_3_out6), .data(rom_39_data));  // open: sel
  ROM #(.addrWidth(24), .dataWidth(32)) rom_40 (.addr(demultiplexer_3_out7), .data(rom_40_data));  // open: sel
  ROM #(.addrWidth(24), .dataWidth(32)) rom_41 (.addr(demultiplexer_3_out8), .data(rom_41_data));  // open: sel
  ROM #(.addrWidth(24), .dataWidth(32)) rom_42 (.addr(demultiplexer_3_out9), .data(rom_42_data));  // open: sel
  ROM #(.addrWidth(24), .dataWidth(32)) rom_43 (.addr(demultiplexer_3_out10), .data(rom_43_data));  // open: sel
  ROM #(.addrWidth(24), .dataWidth(32)) rom_44 (.addr(demultiplexer_3_out11), .data(rom_44_data));  // open: sel
  ROM #(.addrWidth(24), .dataWidth(32)) rom_45 (.addr(demultiplexer_3_out12), .data(rom_45_data));  // open: sel
  ROM #(.addrWidth(24), .dataWidth(32)) rom_46 (.addr(demultiplexer_3_out13), .data(rom_46_data));  // open: sel
  ROM #(.addrWidth(24), .dataWidth(32)) rom_47 (.addr(demultiplexer_3_out14), .data(rom_47_data));  // open: sel
  ROM #(.addrWidth(24), .dataWidth(32)) rom_48 (.addr(demultiplexer_3_out15), .data(rom_48_data));  // open: sel
  ROM #(.addrWidth(24), .dataWidth(32)) rom_49 (.addr(demultiplexer_3_out16), .data(rom_49_data));  // open: sel
  ROM #(.addrWidth(24), .dataWidth(32)) rom_50 (.addr(demultiplexer_3_out17), .data(rom_50_data));  // open: sel
  ROM #(.addrWidth(24), .dataWidth(32)) rom_51 (.addr(demultiplexer_3_out18), .data(rom_51_data));  // open: sel
  ROM #(.addrWidth(24), .dataWidth(32)) rom_52 (.addr(demultiplexer_3_out19), .data(rom_52_data));  // open: sel
  ROM #(.addrWidth(24), .dataWidth(32)) rom_53 (.addr(demultiplexer_3_out20), .data(rom_53_data));  // open: sel
  ROM #(.addrWidth(24), .dataWidth(32)) rom_54 (.addr(demultiplexer_3_out21), .data(rom_54_data));  // open: sel
  ROM #(.addrWidth(24), .dataWidth(32)) rom_55 (.addr(demultiplexer_3_out22), .data(rom_55_data));  // open: sel
  ROM #(.addrWidth(24), .dataWidth(32)) rom_56 (.addr(demultiplexer_3_out23), .data(rom_56_data));  // open: sel
  ROM #(.addrWidth(24), .dataWidth(32)) rom_57 (.addr(demultiplexer_3_out24), .data(rom_57_data));  // open: sel
  ROM #(.addrWidth(24), .dataWidth(32)) rom_58 (.addr(demultiplexer_3_out25), .data(rom_58_data));  // open: sel
  ROM #(.addrWidth(24), .dataWidth(32)) rom_59 (.addr(demultiplexer_3_out26), .data(rom_59_data));  // open: sel
  ROM #(.addrWidth(24), .dataWidth(32)) rom_60 (.addr(demultiplexer_3_out27), .data(rom_60_data));  // open: sel
  ROM #(.addrWidth(24), .dataWidth(32)) rom_61 (.addr(demultiplexer_3_out28), .data(rom_61_data));  // open: sel
  ROM #(.addrWidth(24), .dataWidth(32)) rom_62 (.addr(demultiplexer_3_out29), .data(rom_62_data));  // open: sel
  ROM #(.addrWidth(24), .dataWidth(32)) rom_63 (.addr(demultiplexer_3_out30), .data(rom_63_data));  // open: sel
  ROM #(.addrWidth(24), .dataWidth(32)) rom_64 (.addr(demultiplexer_3_out31), .data(rom_64_data));  // open: sel
  Multiplexer #(.select(5), .width(32)) multiplexer_1 (
    .in0(rom_1_data), .in1(rom_2_data), .in2(rom_3_data), .in3(rom_4_data), .in4(rom_5_data),
    .in5(rom_6_data), .in6(rom_7_data), .in7(rom_8_data), .in8(rom_9_data), .in9(rom_10_data),
    .in10(rom_11_data), .in11(rom_12_data), .in12(rom_13_data), .in13(rom_14_data), .in14(rom_15_data),
    .in15(rom_16_data), .in16(rom_17_data), .in17(rom_18_data), .in18(rom_19_data), .in19(rom_20_data),
    .in20(rom_21_data), .in21(rom_22_data), .in22(rom_23_data), .in23(rom_24_data), .in24(rom_25_data),
    .in25(rom_26_data), .in26(rom_27_data), .in27(rom_28_data), .in28(rom_29_data), .in29(rom_30_data),
    .in30(rom_31_data), .in31(rom_32_data), .out(multiplexer_1_out), .sel(A[30:26]));  // open: en
  Multiplexer #(.select(5), .width(32)) multiplexer_2 (
    .in0(rom_33_data), .in1(rom_34_data), .in2(rom_35_data), .in3(rom_36_data), .in4(rom_37_data),
    .in5(rom_38_data), .in6(rom_39_data), .in7(rom_40_data), .in8(rom_41_data), .in9(rom_42_data),
    .in10(rom_43_data), .in11(rom_44_data), .in12(rom_45_data), .in13(rom_46_data), .in14(rom_47_data),
    .in15(rom_48_data), .in16(rom_49_data), .in17(rom_50_data), .in18(rom_51_data), .in19(rom_52_data),
    .in20(rom_53_data), .in21(rom_54_data), .in22(rom_55_data), .in23(rom_56_data), .in24(rom_57_data),
    .in25(rom_58_data), .in26(rom_59_data), .in27(rom_60_data), .in28(rom_61_data), .in29(rom_62_data),
    .in30(rom_63_data), .in31(rom_64_data), .out(multiplexer_2_out), .sel(A[30:26]));  // open: en
  Multiplexer #(.width(32)) multiplexer_3 (
    .in0(multiplexer_1_out), .in1(multiplexer_2_out), .out(out_2), .sel(A[31]));  // open: en
endmodule
