// Logisim project MIPS.circ as structural Verilog: 2 circuits, main circuit main
module main (
  input  CLR
);

  wire alu_1_zero, and_1_out, button_1_out, CLK, controlunit_1_p1, controlunit_1_p4, delay_1_out_2,
       delay_2_out_2, hazard_detect_1_flushen, hazard_detect_1_if_id_regen, hazard_detect_1_pc_en, not_1_out,
       reg_stage2_1_alusrce, reg_stage2_1_branche, reg_stage2_1_errore, reg_stage2_1_memtorege,
       reg_stage2_1_memwritee, reg_stage2_1_regdste, reg_stage2_1_regwritee, reg_stage3_1_p14,
       reg_stage3_1_p15, reg_stage3_1_p16, reg_stage3_1_p17, reg_stage3_1_p18, reg_stage3_1_p19,
       reg_stage4_1_memtoregw, reg_stage4_1_regwritew;
  wire [1:0] forwarding_unit_1_mux_a, forwarding_unit_1_mux_b;
  wire [3:0] controlunit_1_p11, reg_stage2_1_aluctrle;
  wire [4:0] multiplexer_6_out, multiplexer_7_out, multiplexer_8_out, multiplexer_11_out,
       reg_stage1_1_instrd_2, reg_stage2_1_rde, reg_stage2_1_rse, reg_stage2_1_rte, reg_stage3_1_p22,
       reg_stage4_1_writeregw;
  wire [5:0] controlunit_1_p5;
  wire [9:0] multiplexer_3_out;
  wire [27:0] bit_extender_2_out, shifter_1_out;
  wire [31:0] adder_1_out, adder_2_out, alu_1_alu_result, bit_extender_1_out, data_mem_1_rd, instmem_1_out_2,
       multiplexer_1_out, multiplexer_2_out, multiplexer_4_out, multiplexer_5_out, multiplexer_9_out,
       multiplexer_10_out, multiplexer_12_out, multiplexer_13_out, multiplexer_14_out, multiplexer_15_out,
       PC_q, reg_stage1_1_instrd, reg_stage1_1_pcplus4d, reg_stage2_1_pcplus4e, reg_stage2_1_signimme,
       reg_stage2_1_srcae, reg_stage2_1_srcbe, reg_stage3_1_p20, reg_stage3_1_p21, reg_stage3_1_p23,
       reg_stage4_1_aluoutw, reg_stage4_1_readdataw, regfile32_1_rd1, regfile32_1_rd2, shifter_2_out;

  Clock clock_1 (.out(CLK));
  // Probe on adder_1_out
  Multiplexer #(.width(32)) multiplexer_1 (
    .in0(adder_1_out), .in1(reg_stage3_1_p23), .out(multiplexer_1_out), .sel(and_1_out));  // open: en
  // Probe on reg_stage3_1_p23
  Multiplexer #(.width(32)) multiplexer_2 (
    .in0(multiplexer_1_out), .in1({adder_1_out[31:28], shifter_1_out}), .out(multiplexer_2_out),
    .sel(controlunit_1_p1));  // open: en
  Button button_1 (.out(button_1_out));
  Register #(.width(32)) PC (
    .D(multiplexer_2_out), .en(hazard_detect_1_pc_en), .Q(PC_q), .clk(CLK), .clr(button_1_out));
  InstMem instmem_1 (.A(PC_q), .out_2(instmem_1_out_2));
  Adder #(.width(32)) adder_1 (.a(PC_q), .b(32'h4), .out(adder_1_out));  // open: cin, cout
  Reg_Stage1 reg_stage1_1 (
    .CLR(CLR), .EN(hazard_detect_1_if_id_regen), .CLK(CLK), .InstrF(instmem_1_out_2), .PCPlus4F(adder_1_out),
    .InstrD({reg_stage1_1_instrd[31:26], reg_stage1_1_instrd_2, reg_stage1_1_instrd[20:0]}),
    .PCPlus4D(reg_stage1_1_pcplus4d));
  // ControlUnit controlunit_1: pin names not known; wires that end beside it: controlunit_1_p1, reg_stage1_1_instrd[31:26], reg_stage1_1_instrd[5:0], controlunit_1_p4, controlunit_1_p5[0], controlunit_1_p5[1], controlunit_1_p5[2], controlunit_1_p5[3], controlunit_1_p5[4], controlunit_1_p5[5], controlunit_1_p11
  Delay delay_1 (.in_1(CLK), .out_2(delay_1_out_2));
  Multiplexer #(.width(10)) multiplexer_3 (
    .in0({controlunit_1_p11, controlunit_1_p5}), .in1({10{1'b0}}), .out(multiplexer_3_out),
    .sel(delay_2_out_2));  // open: en
  RegFile32 regfile32_1 (
    .AD1(reg_stage1_1_instrd_2), .AD2(reg_stage1_1_instrd[20:16]), .CLK(delay_1_out_2),
    .WE(reg_stage4_1_regwritew), .AD3(reg_stage4_1_writeregw), .WD3(multiplexer_15_out),
    .RD1(regfile32_1_rd1), .RD2(regfile32_1_rd2));
  assign bit_extender_1_out = {{16{reg_stage1_1_instrd[15]}}, reg_stage1_1_instrd[15:0]};  // Bit_Extender bit_extender_1
  assign bit_extender_2_out = {{2{reg_stage1_1_instrd_2[4]}}, {reg_stage1_1_instrd_2, reg_stage1_1_instrd[20:0]}};  // Bit_Extender bit_extender_2
  Hazard_Detect hazard_detect_1 (
    .ID_EX_MemtoReg(reg_stage2_1_memtorege), .IF_ID_RegRs(reg_stage1_1_instrd_2),
    .ID_EX_RegRt(reg_stage2_1_rte), .IF_ID_RegRt(reg_stage1_1_instrd[20:16]), .PC_En(hazard_detect_1_pc_en),
    .IF_ID_RegEn(hazard_detect_1_if_id_regen), .FlushEn(hazard_detect_1_flushen));
  Delay delay_2 (.in_1(hazard_detect_1_flushen), .out_2(delay_2_out_2));
  Shifter #(.width(28)) shifter_1 (.in(bit_extender_2_out), .\dist (5'b00010), .out(shifter_1_out));
  Multiplexer #(.width(32)) multiplexer_4 (
    .in0(regfile32_1_rd1), .in1({32{1'b0}}), .out(multiplexer_4_out), .sel(delay_2_out_2));  // open: en
  Multiplexer #(.width(32)) multiplexer_5 (
    .in0(regfile32_1_rd2), .in1({32{1'b0}}), .out(multiplexer_5_out), .sel(delay_2_out_2));  // open: en
  Multiplexer #(.width(5)) multiplexer_6 (
    .in0(reg_stage1_1_instrd[20:16]), .in1({5{1'b0}}), .out(multiplexer_6_out), .sel(delay_2_out_2));  // open: en
  Multiplexer #(.width(5)) multiplexer_7 (
    .in0(reg_stage1_1_instrd_2), .in1({5{1'b0}}), .out(multiplexer_7_out), .sel(delay_2_out_2));  // open: en
  Multiplexer #(.width(5)) multiplexer_8 (
    .in0(reg_stage1_1_instrd[15:11]), .in1({5{1'b0}}), .out(multiplexer_8_out), .sel(delay_2_out_2));  // open: en
  Multiplexer #(.width(32)) multiplexer_9 (
    .in0(bit_extender_1_out), .in1({32{1'b0}}), .out(multiplexer_9_out), .sel(delay_2_out_2));  // open: en
  Multiplexer #(.width(32)) multiplexer_10 (
    .in0(reg_stage1_1_pcplus4d), .in1({32{1'b0}}), .out(multiplexer_10_out), .sel(delay_2_out_2));  // open: en
  Reg_Stage2 reg_stage2_1 (
    .CLK(CLK), .CLR(CLR), .EN(1'b1), .ErrorD(controlunit_1_p4), .MemtoRegD(multiplexer_3_out[0]),
    .MemWriteD(multiplexer_3_out[1]), .BranchD(multiplexer_3_out[2]), .ALUSrcD(multiplexer_3_out[3]),
    .RegDstD(multiplexer_3_out[4]), .RegWriteD(multiplexer_3_out[5]), .ALUCtrlD(multiplexer_3_out[9:6]),
    .SrcAD(multiplexer_4_out), .SrcBD(multiplexer_5_out), .RtD(multiplexer_6_out), .RdD(multiplexer_8_out),
    .SignImmD(multiplexer_9_out), .PCPlus4D(multiplexer_10_out), .ErrorE(reg_stage2_1_errore),
    .MemtoRegE(reg_stage2_1_memtorege), .MemWriteE(reg_stage2_1_memwritee), .BranchE(reg_stage2_1_branche),
    .ALUSrcE(reg_stage2_1_alusrce), .RegDstE(reg_stage2_1_regdste), .RegWriteE(reg_stage2_1_regwritee),
    .ALUCtrlE(reg_stage2_1_aluctrle), .SrcAE(reg_stage2_1_srcae), .SrcBE(reg_stage2_1_srcbe),
    .RtE(reg_stage2_1_rte), .RdE(reg_stage2_1_rde), .SignImmE(reg_stage2_1_signimme),
    .PCPlus4E(reg_stage2_1_pcplus4e), .RsD(multiplexer_7_out), .RsE(reg_stage2_1_rse));
  Multiplexer #(.width(5)) multiplexer_11 (
    .in0(reg_stage2_1_rte), .in1(reg_stage2_1_rde), .out(multiplexer_11_out), .sel(reg_stage2_1_regdste));  // open: en
  Multiplexer #(.width(32)) multiplexer_12 (
    .in0(reg_stage2_1_srcbe), .in1(reg_stage2_1_signimme), .out(multiplexer_12_out),
    .sel(reg_stage2_1_alusrce));  // open: en
  Forwarding_Unit forwarding_unit_1 (
    .RegWrite_EX_MEM(reg_stage3_1_p18), .ID_EX_RegRs(reg_stage2_1_rse), .ID_EX_RegRt(reg_stage2_1_rte),
    .MEM_WB_RegRd(reg_stage4_1_writeregw), .MUX_A(forwarding_unit_1_mux_a), .MUX_B(forwarding_unit_1_mux_b),
    .RegWrite_MEM_WB(reg_stage4_1_regwritew), .EX_MEM_RegRd(reg_stage3_1_p22));
  Multiplexer #(.select(2), .width(32)) multiplexer_13 (
    .in0(reg_stage2_1_srcae), .in1(reg_stage3_1_p20), .in2(multiplexer_15_out), .out(multiplexer_13_out),
    .sel(forwarding_unit_1_mux_a));  // open: in3, en
  Multiplexer #(.select(2), .width(32)) multiplexer_14 (
    .in0(multiplexer_12_out), .in1(reg_stage3_1_p20), .in2(multiplexer_15_out), .out(multiplexer_14_out),
    .sel(forwarding_unit_1_mux_b));  // open: in3, en
  ALU alu_1 (
    .SrcA(multiplexer_13_out), .SrcB(multiplexer_14_out), .ALU_Control(reg_stage2_1_aluctrle),
    .Zero(alu_1_zero), .ALU_Result(alu_1_alu_result));
  Shifter #(.width(32)) shifter_2 (.in(reg_stage2_1_signimme), .\dist (5'b00010), .out(shifter_2_out));
  Adder #(.width(32)) adder_2 (.a(shifter_2_out), .b(reg_stage2_1_pcplus4e), .out(adder_2_out));  // open: cin, cout
  // Reg_Stage3 reg_stage3_1: pin names not known; wires that end beside it: reg_stage2_1_errore, reg_stage2_1_memtorege, reg_stage2_1_memwritee, reg_stage2_1_branche, reg_stage2_1_regwritee, alu_1_zero, alu_1_alu_result, reg_stage2_1_srcbe, multiplexer_11_out, adder_2_out, 1'b1, CLK, CLR, reg_stage3_1_p14, reg_stage3_1_p15, reg_stage3_1_p16, reg_stage3_1_p17, reg_stage3_1_p18, reg_stage3_1_p19, reg_stage3_1_p20, reg_stage3_1_p21, reg_stage3_1_p22, reg_stage3_1_p23
  not not_1 (not_1_out, reg_stage3_1_p14);
  and and_1 (and_1_out, not_1_out, reg_stage3_1_p17, reg_stage3_1_p19);
  Data_Mem data_mem_1 (
    .A(reg_stage3_1_p20), .CLK(CLK), .WE(reg_stage3_1_p16), .WD(reg_stage3_1_p21), .RD(data_mem_1_rd));
  Reg_Stage4 reg_stage4_1 (
    .CLR(CLR), .EN(1'b1), .CLK(CLK), .RegWriteM(reg_stage3_1_p18), .MemtoRegM(reg_stage3_1_p15),
    .ALUOutM(reg_stage3_1_p20), .ReadDataM(data_mem_1_rd), .WriteRegM(reg_stage3_1_p22),
    .RegWriteW(reg_stage4_1_regwritew), .MemtoRegW(reg_stage4_1_memtoregw), .ALUOutW(reg_stage4_1_aluoutw),
    .ReadDataW(reg_stage4_1_readdataw), .WriteRegW(reg_stage4_1_writeregw));
  Multiplexer #(.width(32)) multiplexer_15 (
    .in0(reg_stage4_1_aluoutw), .in1(reg_stage4_1_readdataw), .out(multiplexer_15_out),
    .sel(reg_stage4_1_memtoregw));  // open: en
endmodule

module Delay (
  input  in_1,
  output out_2
);

  wire buffer_1_out, buffer_2_out, buffer_3_out, buffer_4_out, buffer_5_out, buffer_6_out, buffer_7_out,
       buffer_8_out, buffer_9_out, buffer_10_out, buffer_11_out, buffer_12_out, buffer_13_out, buffer_14_out,
       buffer_15_out, buffer_16_out, buffer_17_out, buffer_18_out, buffer_19_out, buffer_20_out,
       buffer_21_out, buffer_22_out, buffer_23_out, buffer_24_out, buffer_25_out, buffer_26_out,
       buffer_27_out, buffer_28_out, buffer_29_out, buffer_30_out, buffer_31_out;

  buf buffer_1 (buffer_1_out, buffer_2_out);
  buf buffer_2 (buffer_2_out, in_1);
  buf buffer_3 (buffer_3_out, buffer_5_out);
  buf buffer_4 (buffer_4_out, buffer_3_out);
  buf buffer_5 (buffer_5_out, buffer_1_out);
  buf buffer_6 (buffer_6_out, buffer_4_out);
  buf buffer_7 (buffer_7_out, buffer_6_out);
  buf buffer_8 (buffer_8_out, buffer_10_out);
  buf buffer_9 (buffer_9_out, buffer_8_out);
  buf buffer_10 (buffer_10_out, buffer_7_out);
  buf buffer_11 (buffer_11_out, buffer_12_out);
  buf buffer_12 (buffer_12_out, buffer_14_out);
  buf buffer_13 (buffer_13_out, buffer_9_out);
  buf buffer_14 (buffer_14_out, buffer_13_out);
  buf buffer_15 (buffer_15_out, buffer_17_out);
  buf buffer_16 (buffer_16_out, buffer_18_out);
  buf buffer_17 (buffer_17_out, buffer_11_out);
  buf buffer_18 (buffer_18_out, buffer_15_out);
  buf buffer_19 (buffer_19_out, buffer_16_out);
  buf buffer_20 (buffer_20_out, buffer_19_out);
  buf buffer_21 (buffer_21_out, buffer_20_out);
  buf buffer_22 (buffer_22_out, buffer_21_out);
  buf buffer_23 (buffer_23_out, buffer_24_out);
  buf buffer_24 (buffer_24_out, buffer_22_out);
  buf buffer_25 (buffer_25_out, buffer_26_out);
  buf buffer_26 (buffer_26_out, buffer_23_out);
  buf buffer_27 (buffer_27_out, buffer_29_out);
  buf buffer_28 (buffer_28_out, buffer_25_out);
  buf buffer_29 (buffer_29_out, buffer_30_out);
  buf buffer_30 (buffer_30_out, buffer_28_out);
  buf buffer_31 (buffer_31_out, buffer_27_out);
  buf buffer_32 (out_2, buffer_31_out);
endmodule
