// Logisim project Main_Decoder.circ as structural Verilog: 1 circuit, main circuit Main_Decoder
module Main_Decoder (
  input  [5:0] Op_5_0,
  output MemtoReg,
  output MemWrite,
  output Branch,
  output ALUSrc,
  output RegDst,
  output RegWrite,
  output Jump,
  output [1:0] ALUOp_1_0
);

  wire and_4_out, and_5_out, and_6_out, and_8_out, not_1_out, not_2_out, not_3_out, not_4_out, not_5_out,
       not_6_out, not_7_out, not_8_out, not_9_out, not_10_out, not_11_out, not_12_out, not_13_out,
       not_14_out, not_15_out, not_16_out, not_17_out, not_18_out, not_19_out;

  not not_1 (not_1_out, Op_5_0[4]);
  not not_2 (not_2_out, Op_5_0[2]);
  not not_3 (not_3_out, Op_5_0[3]);
  or or_1 (ALUSrc, Op_5_0[1], Op_5_0[3]);
  not not_4 (not_4_out, Op_5_0[3]);
  not not_5 (not_5_out, Op_5_0[1]);
  not not_6 (not_6_out, Op_5_0[5]);
  not not_7 (not_7_out, Op_5_0[4]);
  not not_8 (not_8_out, Op_5_0[2]);
  not not_9 (not_9_out, Op_5_0[1]);
  not not_10 (not_10_out, Op_5_0[0]);
  not not_11 (not_11_out, Op_5_0[4]);
  not not_12 (not_12_out, Op_5_0[3]);
  not not_13 (not_13_out, Op_5_0[2]);
  not not_14 (not_14_out, Op_5_0[1]);
  not not_15 (not_15_out, Op_5_0[0]);
  not not_16 (not_16_out, Op_5_0[0]);
  not not_17 (not_17_out, Op_5_0[3]);
  not not_18 (not_18_out, Op_5_0[2]);
  not not_19 (not_19_out, Op_5_0[1]);
  and and_1 (MemWrite, Op_5_0[5], not_1_out, Op_5_0[3], not_2_out, Op_5_0[1], Op_5_0[0]);
  and and_2 (Branch, not_3_out, Op_5_0[2]);
  and and_3 (RegDst, not_4_out, not_5_out);
  and and_4 (and_4_out, not_6_out, not_7_out, not_8_out, not_9_out, not_10_out);
  and and_5 (and_5_out, Op_5_0[5], not_11_out, not_12_out, not_13_out, Op_5_0[1], Op_5_0[0]);
  and and_6 (and_6_out, Op_5_0[5], Op_5_0[4], Op_5_0[3], Op_5_0[2], not_14_out, not_15_out);
  and and_7 (Jump, Op_5_0[1], not_16_out);
  and and_8 (and_8_out, not_17_out, not_18_out, not_19_out);
  or or_2 (RegWrite, and_4_out, and_5_out, and_6_out);
  or or_3 (ALUOp_1_0[1], and_8_out, Op_5_0[4]);

  assign ALUOp_1_0[0] = Op_5_0[2];
  assign MemtoReg = Op_5_0[1];
endmodule
