// Logisim project Pipeline_Reg.circ as structural Verilog: 4 circuits, main circuit Reg_Stage1
// IF/DE
module Reg_Stage1 (
  input  CLR,
  input  EN,
  input  CLK,
  input  [31:0] InstrF,
  input  [31:0] PCPlus4F,
  input  [31:0] PC,
  output [31:0] InstrD,
  output [31:0] PCPlus4D,
  output [31:0] PC_2
);

  wire [31:0] multiplexer_1_out, multiplexer_2_out, multiplexer_3_out;

  Multiplexer #(.width(32)) multiplexer_1 (
    .in0(InstrF), .in1({32{1'b0}}), .out(multiplexer_1_out), .sel(CLR));  // open: en
  Multiplexer #(.width(32)) multiplexer_2 (
    .in0(PCPlus4F), .in1({32{1'b0}}), .out(multiplexer_2_out), .sel(CLR));  // open: en
  Multiplexer #(.width(32)) multiplexer_3 (.in0(PC), .in1({32{1'b0}}), .out(multiplexer_3_out), .sel(CLR));  // open: en
  Register #(.width(32)) register_1 (.D(multiplexer_1_out), .en(EN), .Q(InstrD), .clk(CLK));  // open: clr
  Register #(.width(32)) register_2 (.D(multiplexer_2_out), .en(EN), .Q(PCPlus4D), .clk(CLK));  // open: clr
  Register #(.width(32)) register_3 (.D(multiplexer_3_out), .en(EN), .Q(PC_2), .clk(CLK));  // open: clr
endmodule

// DE/EX
module Reg_Stage2 (
  input  CLK,
  input  CLR,
  input  MemtoRegD,
  input  MemWriteD,
  input  ALUSrcD,
  input  RegDstD,
  input  RegWriteD,
  input  [3:0] ALUCtrlD,
  input  [31:0] SrcAD,
  input  [31:0] SrcBD,
  input  [4:0] RsD,
  input  [4:0] RtD,
  input  [4:0] RdD,
  input  [31:0] SignImmD,
  output MemtoRegE,
  output MemWriteE,
  output ALUSrcE,
  output RegDstE,
  output RegWriteE,
  output [3:0] ALUCtrlE,
  output [31:0] SrcAE,
  output [31:0] SrcBE,
  output [4:0] RsE,
  output [4:0] RtE,
  output [4:0] RdE,
  output [31:0] SignImmE
);

  Register #(.width(1)) register_1 (.D(MemtoRegD), .en(1'b1), .Q(MemtoRegE), .clk(CLK), .clr(CLR));
  Register #(.width(1)) register_2 (.D(MemWriteD), .en(1'b1), .Q(MemWriteE), .clk(CLK), .clr(CLR));
  Register #(.width(1)) register_3 (.D(ALUSrcD), .en(1'b1), .Q(ALUSrcE), .clk(CLK), .clr(CLR));
  Register #(.width(1)) register_4 (.D(RegDstD), .en(1'b1), .Q(RegDstE), .clk(CLK), .clr(CLR));
  Register #(.width(1)) register_5 (.D(RegWriteD), .en(1'b1), .Q(RegWriteE), .clk(CLK), .clr(CLR));
  Register #(.width(4)) register_6 (.D(ALUCtrlD), .en(1'b1), .Q(ALUCtrlE), .clk(CLK), .clr(CLR));
  Register #(.width(32)) register_7 (.D(SrcAD), .en(1'b1), .Q(SrcAE), .clk(CLK), .clr(CLR));
  Register #(.width(32)) register_8 (.D(SrcBD), .en(1'b1), .Q(SrcBE), .clk(CLK), .clr(CLR));
  Register #(.width(5)) register_9 (.D(RsD), .en(1'b1), .Q(RsE), .clk(CLK), .clr(CLR));
  Register #(.width(5)) register_10 (.D(RtD), .en(1'b1), .Q(RtE), .clk(CLK), .clr(CLR));
  Register #(.width(5)) register_11 (.D(RdD), .en(1'b1), .Q(RdE), .clk(CLK), .clr(CLR));
  Register #(.width(32)) register_12 (.D(SignImmD), .en(1'b1), .Q(SignImmE), .clk(CLK), .clr(CLR));
endmodule

// EX/MEM
module Reg_Stage3 (
  input  CLK,
  input  RegWriteE,
  input  MemtoRegE,
  input  MemWriteE,
  input  [31:0] ALUOutE,
  input  [31:0] WriteDataE,
  input  [4:0] WriteRegE,
  output RegWriteM,
  output MemtoRegM,
  output MemWriteM,
  output [31:0] ALUOutM,
  output [31:0] WriteDataM,
  output [4:0] WriteRegM
);

  Register #(.width(1)) register_1 (.D(RegWriteE), .en(1'b1), .Q(RegWriteM), .clk(CLK), .clr(1'b0));
  Register #(.width(1)) register_2 (.D(MemtoRegE), .en(1'b1), .Q(MemtoRegM), .clk(CLK), .clr(1'b0));
  Register #(.width(1)) register_3 (.D(MemWriteE), .en(1'b1), .Q(MemWriteM), .clk(CLK), .clr(1'b0));
  Register #(.width(32)) register_4 (.D(ALUOutE), .en(1'b1), .Q(ALUOutM), .clk(CLK), .clr(1'b0));
  Register #(.width(32)) register_5 (.D(WriteDataE), .en(1'b1), .Q(WriteDataM), .clk(CLK), .clr(1'b0));
  Register #(.width(5)) register_6 (.D(WriteRegE), .en(1'b1), .Q(WriteRegM), .clk(CLK), .clr(1'b0));
endmodule

// MEM/WB
module Reg_Stage4 (
  input  CLK,
  input  RegWriteM,
  input  MemtoRegM,
  input  [31:0] ALUOutM,
  input  [31:0] ReadDataM,
  input  [4:0] WriteRegM,
  output RegWriteW,
  output MemtoRegW,
  output [31:0] ALUOutW,
  output [31:0] ReadDataW,
  output [4:0] WriteRegW
);

  Register #(.width(1)) register_1 (.D(RegWriteM), .en(1'b1), .Q(RegWriteW), .clk(CLK), .clr(1'b0));
  Register #(.width(1)) register_2 (.D(MemtoRegM), .en(1'b1), .Q(MemtoRegW), .clk(CLK), .clr(1'b0));
  Register #(.width(32)) register_3 (.D(ALUOutM), .en(1'b1), .Q(ALUOutW), .clk(CLK), .clr(1'b0));
  Register #(.width(32)) register_4 (.D(ReadDataM), .en(1'b1), .Q(ReadDataW), .clk(CLK), .clr(1'b0));
  Register #(.width(5)) register_5 (.D(WriteRegM), .en(1'b1), .Q(WriteRegW), .clk(CLK), .clr(1'b0));
endmodule
