// Logisim project PopCounter.circ as structural Verilog: 3 circuits, main circuit PopCounter4
module PopCounter4 (
  input  [3:0] in_1,
  output [3:0] out_2
);

  wire [3:0] adder_1_out, adder_2_out, bit_extender_1_out, bit_extender_2_out, bit_extender_3_out,
       bit_extender_4_out;

  assign bit_extender_1_out = {{3{1'b0}}, in_1[0]};  // Bit_Extender bit_extender_1
  assign bit_extender_2_out = {{3{1'b0}}, in_1[1]};  // Bit_Extender bit_extender_2
  assign bit_extender_3_out = {{3{1'b0}}, in_1[2]};  // Bit_Extender bit_extender_3
  assign bit_extender_4_out = {{3{1'b0}}, in_1[3]};  // Bit_Extender bit_extender_4
  Adder #(.width(4)) adder_1 (.a(bit_extender_1_out), .b(bit_extender_2_out), .out(adder_1_out));  // open: cin, cout
  Adder #(.width(4)) adder_2 (.a(bit_extender_3_out), .b(bit_extender_4_out), .out(adder_2_out));  // open: cin, cout
  Adder #(.width(4)) adder_3 (.a(adder_1_out), .b(adder_2_out), .out(out_2));  // open: cin, cout
endmodule

module PopCounter16 (
  input  [15:0] in_1,
  output [15:0] out_2
);

  wire [3:0] popcounter4_1_out_2, popcounter4_2_out_2, popcounter4_3_out_2, popcounter4_4_out_2;
  wire [15:0] adder_1_out, adder_2_out, bit_extender_1_out, bit_extender_2_out, bit_extender_3_out,
       bit_extender_4_out;

  PopCounter4 popcounter4_1 (.in_1(in_1[3:0]), .out_2(popcounter4_1_out_2));
  PopCounter4 popcounter4_2 (.in_1(in_1[7:4]), .out_2(popcounter4_2_out_2));
  PopCounter4 popcounter4_3 (.in_1(in_1[11:8]), .out_2(popcounter4_3_out_2));
  PopCounter4 popcounter4_4 (.in_1(in_1[15:12]), .out_2(popcounter4_4_out_2));
  assign bit_extender_1_out = {{12{1'b0}}, popcounter4_1_out_2};  // Bit_Extender bit_extender_1
  assign bit_extender_2_out = {{12{1'b0}}, popcounter4_2_out_2};  // Bit_Extender bit_extender_2
  assign bit_extender_3_out = {{12{1'b0}}, popcounter4_3_out_2};  // Bit_Extender bit_extender_3
  assign bit_extender_4_out = {{12{1'b0}}, popcounter4_4_out_2};  // Bit_Extender bit_extender_4
  Adder #(.width(16)) adder_1 (.a(bit_extender_1_out), .b(bit_extender_2_out), .out(adder_1_out));  // open: cin, cout
  Adder #(.width(16)) adder_2 (.a(bit_extender_3_out), .b(bit_extender_4_out), .out(adder_2_out));  // open: cin, cout
  Adder #(.width(16)) adder_3 (.a(adder_1_out), .b(adder_2_out), .out(out_2));  // open: cin, cout
endmodule

module PopCounter32 (
  input  [31:0] in_1,
  output [31:0] out_2
);

  wire [15:0] popcounter16_1_out_2, popcounter16_2_out_2;
  wire [31:0] bit_extender_1_out, bit_extender_2_out;

  PopCounter16 popcounter16_1 (.in_1(in_1[15:0]), .out_2(popcounter16_1_out_2));
  PopCounter16 popcounter16_2 (.in_1(in_1[31:16]), .out_2(popcounter16_2_out_2));
  assign bit_extender_1_out = {{16{1'b0}}, popcounter16_1_out_2};  // Bit_Extender bit_extender_1
  assign bit_extender_2_out = {{16{1'b0}}, popcounter16_2_out_2};  // Bit_Extender bit_extender_2
  Adder #(.width(32)) adder_1 (.a(bit_extender_1_out), .b(bit_extender_2_out), .out(out_2));  // open: cin, cout
endmodule
