// Logisim project RegFile.circ as structural Verilog: 3 circuits, main circuit RegFile4
module RegFile4 (
  input  [1:0] AD1,
  input  [1:0] AD2,
  input  CLK,
  input  [31:0] WD3,
  input  [1:0] AD3,
  input  WE,
  output [31:0] RD1,
  output [31:0] RD2
);

  wire demultiplexer_2_out0, demultiplexer_2_out1, demultiplexer_2_out2, demultiplexer_2_out3;
  wire [31:0] demultiplexer_1_out0, demultiplexer_1_out1, demultiplexer_1_out2, demultiplexer_1_out3,
       register_1_q, register_2_q, register_3_q, register_4_q;

  Demultiplexer #(.select(2), .width(32)) demultiplexer_1 (
    .out0(demultiplexer_1_out0), .out1(demultiplexer_1_out1), .out2(demultiplexer_1_out2),
    .out3(demultiplexer_1_out3), .in(WD3), .sel(AD3));  // open: en
  Demultiplexer #(.select(2), .disabled(0)) demultiplexer_2 (
    .out0(demultiplexer_2_out0), .out1(demultiplexer_2_out1), .out2(demultiplexer_2_out2),
    .out3(demultiplexer_2_out3), .in(WE), .sel(AD3));  // open: en
  Register #(.width(32)) register_1 (
    .D(demultiplexer_1_out0), .en(demultiplexer_2_out0), .Q(register_1_q), .clk(CLK));  // open: clr
  Register #(.width(32)) register_2 (
    .D(demultiplexer_1_out1), .en(demultiplexer_2_out1), .Q(register_2_q), .clk(CLK));  // open: clr
  Register #(.width(32)) register_3 (
    .D(demultiplexer_1_out2), .en(demultiplexer_2_out2), .Q(register_3_q), .clk(CLK));  // open: clr
  Register #(.width(32)) register_4 (
    .D(demultiplexer_1_out3), .en(demultiplexer_2_out3), .Q(register_4_q), .clk(CLK));  // open: clr
  Multiplexer #(.select(2), .width(32)) multiplexer_1 (
    .in0(register_1_q), .in1(register_2_q), .in2(register_3_q), .in3(register_4_q), .out(RD1), .sel(AD1));  // open: en
  Multiplexer #(.select(2), .width(32)) multiplexer_2 (
    .in0(register_1_q), .in1(register_2_q), .in2(register_3_q), .in3(register_4_q), .out(RD2), .sel(AD2));  // open: en
endmodule

module RegFile16 (
  input  WE,
  input  CLK,
  input  [3:0] AD1,
  input  [3:0] AD2,
  input  [3:0] AD3,
  input  [31:0] WD3,
  output [31:0] RD1,
  output [31:0] RD2
);

  wire demultiplexer_1_out0, demultiplexer_1_out1, demultiplexer_1_out2, demultiplexer_1_out3;
  wire [31:0] demultiplexer_2_out0, demultiplexer_2_out1, demultiplexer_2_out2, demultiplexer_2_out3,
       regfile4_1_rd1, regfile4_1_rd2, regfile4_2_rd1, regfile4_2_rd2, regfile4_3_rd1, regfile4_3_rd2,
       regfile4_4_rd1, regfile4_4_rd2;

  Demultiplexer #(.select(2), .disabled(0)) demultiplexer_1 (
    .out0(demultiplexer_1_out0), .out1(demultiplexer_1_out1), .out2(demultiplexer_1_out2),
    .out3(demultiplexer_1_out3), .in(WE), .sel(AD3[3:2]));  // open: en
  Demultiplexer #(.select(2), .width(32)) demultiplexer_2 (
    .out0(demultiplexer_2_out0), .out1(demultiplexer_2_out1), .out2(demultiplexer_2_out2),
    .out3(demultiplexer_2_out3), .in(WD3), .sel(AD3[3:2]));  // open: en
  RegFile4 regfile4_1 (
    .AD1(AD1[1:0]), .AD2(AD2[1:0]), .CLK(CLK), .WD3(demultiplexer_2_out0), .AD3(AD3[1:0]),
    .WE(demultiplexer_1_out0), .RD1(regfile4_1_rd1), .RD2(regfile4_1_rd2));
  RegFile4 regfile4_2 (
    .AD1(AD1[1:0]), .AD2(AD2[1:0]), .CLK(CLK), .WD3(demultiplexer_2_out1), .AD3(AD3[1:0]),
    .WE(demultiplexer_1_out1), .RD1(regfile4_2_rd1), .RD2(regfile4_2_rd2));
  RegFile4 regfile4_3 (
    .AD1(AD1[1:0]), .AD2(AD2[1:0]), .CLK(CLK), .WD3(demultiplexer_2_out2), .AD3(AD3[1:0]),
    .WE(demultiplexer_1_out2), .RD1(regfile4_3_rd1), .RD2(regfile4_3_rd2));
  RegFile4 regfile4_4 (
    .AD1(AD1[1:0]), .AD2(AD2[1:0]), .CLK(CLK), .WD3(demultiplexer_2_out3), .AD3(AD3[1:0]),
    .WE(demultiplexer_1_out3), .RD1(regfile4_4_rd1), .RD2(regfile4_4_rd2));
  Multiplexer #(.select(2), .width(32)) multiplexer_1 (
    .in0(regfile4_1_rd1), .in1(regfile4_2_rd1), .in2(regfile4_3_rd1), .in3(regfile4_4_rd1), .out(RD1),
    .sel(AD1[3:2]));  // open: en
  Multiplexer #(.select(2), .width(32)) multiplexer_2 (
    .in0(regfile4_1_rd2), .in1(regfile4_2_rd2), .in2(regfile4_3_rd2), .in3(regfile4_4_rd2), .out(RD2),
    .sel(AD2[3:2]));  // open: en
endmodule

// RegFile
module RegFile32 (
  input  [4:0] AD1,
  input  [4:0] AD2,
  input  CLK,
  input  WE,
  input  [4:0] AD3,
  input  [31:0] WD3,
  output [31:0] RD1,
  output [31:0] RD2
);

  wire demultiplexer_1_out0, demultiplexer_1_out1;
  wire [31:0] demultiplexer_2_out0, demultiplexer_2_out1, regfile16_1_rd1, regfile16_1_rd2, regfile16_2_rd1,
       regfile16_2_rd2;

  Demultiplexer #(.disabled(0)) demultiplexer_1 (
    .out0(demultiplexer_1_out0), .out1(demultiplexer_1_out1), .in(WE), .sel(AD3[4]));  // open: en
  Demultiplexer #(.width(32)) demultiplexer_2 (
    .out0(demultiplexer_2_out0), .out1(demultiplexer_2_out1), .in(WD3), .sel(AD3[4]));  // open: en
  RegFile16 regfile16_1 (
    .WE(demultiplexer_1_out0), .CLK(CLK), .AD1(AD1[3:0]), .AD2(AD2[3:0]), .AD3(AD3[3:0]),
    .WD3(demultiplexer_2_out0), .RD1(regfile16_1_rd1), .RD2(regfile16_1_rd2));
  RegFile16 regfile16_2 (
    .WE(demultiplexer_1_out1), .CLK(CLK), .AD1(AD1[3:0]), .AD2(AD2[3:0]), .AD3(AD3[3:0]),
    .WD3(demultiplexer_2_out1), .RD1(regfile16_2_rd1), .RD2(regfile16_2_rd2));
  Multiplexer #(.width(32)) multiplexer_1 (
    .in0(regfile16_1_rd1), .in1(regfile16_2_rd1), .out(RD1), .sel(AD1[4]));  // open: en
  Multiplexer #(.width(32)) multiplexer_2 (
    .in0(regfile16_1_rd2), .in1(regfile16_2_rd2), .out(RD2), .sel(AD2[4]));  // open: en
endmodule
