// Logisim project Reg_Stage1.circ as structural Verilog: 1 circuit, main circuit Reg_Stage1
module Reg_Stage1 (
  input  CLR,
  input  EN,
  input  CLK,
  input  [31:0] InstrF,
  input  [31:0] PCPlus4F,
  output [31:0] InstrD,
  output [31:0] PCPlus4D
);

  Register #(.width(32)) register_1 (.D(InstrF), .en(EN), .Q(InstrD), .clk(CLK), .clr(CLR));
  Register #(.width(32)) register_2 (.D(PCPlus4F), .en(EN), .Q(PCPlus4D), .clk(CLK), .clr(CLR));
endmodule
