// Logisim project Reg_Stage2.circ as structural Verilog: 1 circuit, main circuit Reg_Stage2
module Reg_Stage2 (
  input  CLK,
  input  CLR,
  input  EN,
  input  ErrorD,
  input  MemtoRegD,
  input  MemWriteD,
  input  BranchD,
  input  ALUSrcD,
  input  RegDstD,
  input  RegWriteD,
  input  [3:0] ALUCtrlD,
  input  [31:0] SrcAD,
  input  [31:0] SrcBD,
  input  [4:0] RsD,
  input  [4:0] RtD,
  input  [4:0] RdD,
  input  [31:0] SignImmD,
  input  [31:0] PCPlus4D,
  output ErrorE,
  output MemtoRegE,
  output MemWriteE,
  output BranchE,
  output ALUSrcE,
  output RegDstE,
  output RegWriteE,
  output [3:0] ALUCtrlE,
  output [31:0] SrcAE,
  output [31:0] SrcBE,
  output [4:0] RsE,
  output [4:0] RtE,
  output [4:0] RdE,
  output [31:0] SignImmE,
  output [31:0] PCPlus4E
);

  Register #(.width(1)) register_1 (.D(ErrorD), .en(EN), .Q(ErrorE), .clk(CLK), .clr(CLR));
  Register #(.width(1)) register_2 (.D(MemtoRegD), .en(EN), .Q(MemtoRegE), .clk(CLK), .clr(CLR));
  Register #(.width(1)) register_3 (.D(MemWriteD), .en(EN), .Q(MemWriteE), .clk(CLK), .clr(CLR));
  Register #(.width(1)) register_4 (.D(BranchD), .en(EN), .Q(BranchE), .clk(CLK), .clr(CLR));
  Register #(.width(1)) register_5 (.D(ALUSrcD), .en(EN), .Q(ALUSrcE), .clk(CLK), .clr(CLR));
  Register #(.width(1)) register_6 (.D(RegDstD), .en(EN), .Q(RegDstE), .clk(CLK), .clr(CLR));
  Register #(.width(1)) register_7 (.D(RegWriteD), .en(EN), .Q(RegWriteE), .clk(CLK), .clr(CLR));
  Register #(.width(4)) register_8 (.D(ALUCtrlD), .en(EN), .Q(ALUCtrlE), .clk(CLK), .clr(CLR));
  Register #(.width(32)) register_9 (.D(SrcAD), .en(EN), .Q(SrcAE), .clk(CLK), .clr(CLR));
  Register #(.width(32)) register_10 (.D(SrcBD), .en(EN), .Q(SrcBE), .clk(CLK), .clr(CLR));
  Register #(.width(5)) register_11 (.D(RsD), .en(EN), .Q(RsE), .clk(CLK), .clr(CLR));
  Register #(.width(5)) register_12 (.D(RtD), .en(EN), .Q(RtE), .clk(CLK), .clr(CLR));
  Register #(.width(5)) register_13 (.D(RdD), .en(EN), .Q(RdE), .clk(CLK), .clr(CLR));
  Register #(.width(32)) register_14 (.D(SignImmD), .en(EN), .Q(SignImmE), .clk(CLK), .clr(CLR));
  Register #(.width(32)) register_15 (.D(PCPlus4D), .en(EN), .Q(PCPlus4E), .clk(CLK), .clr(CLR));
endmodule
