// Logisim project Reg_Stage3.circ as structural Verilog: 1 circuit, main circuit Reg_Stage3
module Reg_Stage3 (
  input  CLR,
  input  EN,
  input  CLK,
  input  ErrorE,
  input  RegWriteE,
  input  MemtoRegE,
  input  MemWriteE,
  input  BranchE,
  input  ZeroE,
  input  [31:0] ALUOutE,
  input  [31:0] WriteDataE,
  input  [4:0] WriteRegE,
  input  [31:0] PCBranchE,
  output ErrorM,
  output RegWriteM,
  output MemtoRegM,
  output MemWriteM,
  output BranchM,
  output ZeroM,
  output [31:0] ALUOutM,
  output [31:0] WriteDataM,
  output [4:0] WriteRegM,
  output [31:0] PCBranchM
);

  Register #(.width(1)) register_1 (.D(ErrorE), .en(EN), .Q(ErrorM), .clk(CLK), .clr(CLR));
  Register #(.width(1)) register_2 (.D(RegWriteE), .en(EN), .Q(RegWriteM), .clk(CLK), .clr(CLR));
  Register #(.width(1)) register_3 (.D(MemtoRegE), .en(EN), .Q(MemtoRegM), .clk(CLK), .clr(CLR));
  Register #(.width(1)) register_4 (.D(MemWriteE), .en(EN), .Q(MemWriteM), .clk(CLK), .clr(CLR));
  Register #(.width(1)) register_5 (.D(BranchE), .en(EN), .Q(BranchM), .clk(CLK), .clr(CLR));
  Register #(.width(1)) register_6 (.D(ZeroE), .en(EN), .Q(ZeroM), .clk(CLK), .clr(CLR));
  Register #(.width(32)) register_7 (.D(ALUOutE), .en(EN), .Q(ALUOutM), .clk(CLK), .clr(CLR));
  Register #(.width(32)) register_8 (.D(WriteDataE), .en(EN), .Q(WriteDataM), .clk(CLK), .clr(CLR));
  Register #(.width(5)) register_9 (.D(WriteRegE), .en(EN), .Q(WriteRegM), .clk(CLK), .clr(CLR));
  Register #(.width(32)) register_10 (.D(PCBranchE), .en(EN), .Q(PCBranchM), .clk(CLK), .clr(CLR));
endmodule
