// Logisim project Reg_Stage4.circ as structural Verilog: 1 circuit, main circuit Reg_Stage4
module Reg_Stage4 (
  input  CLR,
  input  EN,
  input  CLK,
  input  RegWriteM,
  input  MemtoRegM,
  input  [31:0] ALUOutM,
  input  [31:0] ReadDataM,
  input  [4:0] WriteRegM,
  output RegWriteW,
  output MemtoRegW,
  output [31:0] ALUOutW,
  output [31:0] ReadDataW,
  output [4:0] WriteRegW
);

  Register #(.width(1)) register_1 (.D(RegWriteM), .en(EN), .Q(RegWriteW), .clk(CLK), .clr(CLR));
  Register #(.width(1)) register_2 (.D(MemtoRegM), .en(EN), .Q(MemtoRegW), .clk(CLK), .clr(CLR));
  Register #(.width(32)) register_3 (.D(ALUOutM), .en(EN), .Q(ALUOutW), .clk(CLK), .clr(CLR));
  Register #(.width(32)) register_4 (.D(ReadDataM), .en(EN), .Q(ReadDataW), .clk(CLK), .clr(CLR));
  Register #(.width(5)) register_5 (.D(WriteRegM), .en(EN), .Q(WriteRegW), .clk(CLK), .clr(CLR));
endmodule
